// Logisim project cpu.circ as structural Verilog: 17 circuits, main circuit main
module main (
);

  wire alsu_1_cout, and_1_out, and_2_out, button_1_out, button_2_out, button_3_out, clock_1_out,
       keyboard_1_avail, n74175_1_pin1, n74175_1_pin2, n74175_1_pin9, n74175_1_pin16, n74175_2_pin2,
       n74175_2_pin4, or_1_out, unitOfControl_acclr, unitOfControl_acincr, unitOfControl_acload,
       unitOfControl_alsus0, unitOfControl_alsus1, unitOfControl_alsus2, unitOfControl_alsus3,
       unitOfControl_alsuselector, unitOfControl_arincr, unitOfControl_arld, unitOfControl_bs0,
       unitOfControl_bs1, unitOfControl_bs2, unitOfControl_bs3, unitOfControl_drincr, unitOfControl_drload,
       unitOfControl_eclr, unitOfControl_eload, unitOfControl_inputflush, unitOfControl_irld,
       unitOfControl_loadb9, unitOfControl_mltdrinrin, unitOfControl_outrload, unitOfControl_pcincr,
       unitOfControl_pcload, unitOfControl_ramread, unitOfControl_ramwrite, unitOfControl_romread,
       unitOfControl_romwrite, unitOfControl_trload;
  wire [3:0] AC_bitsout, AC_bitsout_2, AC_bitsout_3, AC_bitsout_4, ledbar_7_p1, ram_1_dout, ram_1_dout_2,
       ram_1_dout_3, ram_1_dout_4, sixteentwotoonemultiplexer_1_dataout,
       sixteentwotoonemultiplexer_1_dataout_2, sixteentwotoonemultiplexer_1_dataout_3,
       sixteentwotoonemultiplexer_1_dataout_4, sixteentwotoonemultiplexer_2_dataout,
       sixteentwotoonemultiplexer_2_dataout_2, sixteentwotoonemultiplexer_2_dataout_3,
       sixteentwotoonemultiplexer_2_dataout_4, TR_bitsout, TR_bitsout_2, TR_bitsout_3, TR_bitsout_4;
  wire [6:0] keyboard_1_data, OUTR_bitsout;
  wire [10:0] AR_bitsout;
  wire [11:0] addressOfInterruptFunction_bitsout, PC_bitsout;
  wire [11:11] AR_bitsout_2;
  wire [15:0] BUSMULTIPLEXER_dataout, IR_bitsout, ledbar_2_p1, ledbar_3_p1, ledbar_5_p2, ram_2_dout,
       sixteeneightwithzerotoonemultiplexr_1_dataout, sixteentwotoonemultiplexer_3_dataout;
  wire [15:15] n74175_1_pin8;

  Clock clock_1 (.out(clock_1_out));
  Keyboard #(.buflen(1)) keyboard_1 (
    .clr(unitOfControl_inputflush), .avail(keyboard_1_avail), .data(keyboard_1_data));  // open: clk, re
  Hex_Digit_Display hex_digit_display_1 (.value(sixteentwotoonemultiplexer_2_dataout_4));  // open: dp
  Hex_Digit_Display hex_digit_display_2 (.value(sixteentwotoonemultiplexer_2_dataout_3));  // open: dp
  sixteenTwoToOneMultiplexer sixteentwotoonemultiplexer_1 (
    .ENActiveHigh(n74175_1_pin16), .GND(n74175_1_pin8[15]), .VCC(n74175_1_pin16),
    .S0(unitOfControl_alsuselector), .INPUT0(sixteentwotoonemultiplexer_3_dataout),
    .INPUT1({AC_bitsout_4, AC_bitsout_3, AC_bitsout_2, AC_bitsout}),
    .DATAOUT({sixteentwotoonemultiplexer_1_dataout_4, sixteentwotoonemultiplexer_1_dataout_3, sixteentwotoonemultiplexer_1_dataout_2, sixteentwotoonemultiplexer_1_dataout}));
  Hex_Digit_Display hex_digit_display_3 (.value(sixteentwotoonemultiplexer_2_dataout_2));  // open: dp
  Hex_Digit_Display hex_digit_display_4 (.value(sixteentwotoonemultiplexer_2_dataout));  // open: dp
  Hex_Digit_Display hex_digit_display_5 (.value(sixteentwotoonemultiplexer_1_dataout_4));  // open: dp
  Hex_Digit_Display hex_digit_display_6 (.value(sixteentwotoonemultiplexer_1_dataout_3));  // open: dp
  Hex_Digit_Display hex_digit_display_7 (.value(sixteentwotoonemultiplexer_1_dataout_2));  // open: dp
  Hex_Digit_Display hex_digit_display_8 (.value(sixteentwotoonemultiplexer_1_dataout));  // open: dp
  sixteenTwoToOneMultiplexer sixteentwotoonemultiplexer_2 (
    .ENActiveHigh(n74175_1_pin16), .GND(n74175_1_pin8[15]), .VCC(n74175_1_pin16),
    .S0(unitOfControl_alsuselector), .INPUT0({AC_bitsout_4, AC_bitsout_3, AC_bitsout_2, AC_bitsout}),
    .INPUT1(sixteentwotoonemultiplexer_3_dataout),
    .DATAOUT({sixteentwotoonemultiplexer_2_dataout_4, sixteentwotoonemultiplexer_2_dataout_3, sixteentwotoonemultiplexer_2_dataout_2, sixteentwotoonemultiplexer_2_dataout}));
  sixteenTwoToOneMultiplexer sixteentwotoonemultiplexer_3 (
    .ENActiveHigh(n74175_1_pin16), .GND(n74175_1_pin8[15]), .VCC(n74175_1_pin16),
    .S0(unitOfControl_mltdrinrin), .INPUT0({{9{n74175_1_pin8[15]}}, keyboard_1_data}), .INPUT1(ledbar_5_p2),
    .DATAOUT(sixteentwotoonemultiplexer_3_dataout));
  // LedBar #(.inputtype("row"), .matrixcols(16)) ledbar_1: pin names not known; wires that end beside it: sixteentwotoonemultiplexer_3_dataout
  or or_1 (or_1_out, button_2_out, button_1_out);
  Button button_1 (.out(button_1_out));
  RAM #(.addrWidth(11), .asyncread("true"), .dataWidth(16), .\type ("nonvolatile")) ram_1 (
    .addr(AR_bitsout), .we(unitOfControl_romwrite), .oe(unitOfControl_romread), .clk(clock_1_out),
    .din(ledbar_2_p1), .dout({ram_1_dout_4, ram_1_dout_3, ram_1_dout_2, ram_1_dout}));
  // LedBar #(.inputtype("row"), .matrixcols(16)) ledbar_2: pin names not known; wires that end beside it: ledbar_2_p1
  // LedBar #(.inputtype("row"), .matrixcols(16)) ledbar_3: pin names not known; wires that end beside it: ledbar_3_p1
  ALSU alsu_1 (
    .VCC(n74175_1_pin16), .GND(n74175_1_pin8[15]), .S3(unitOfControl_alsus3), .S2(unitOfControl_alsus2),
    .S1(unitOfControl_alsus1), .S0(unitOfControl_alsus0),
    .BIN({sixteentwotoonemultiplexer_1_dataout_4, sixteentwotoonemultiplexer_1_dataout_3, sixteentwotoonemultiplexer_1_dataout_2, sixteentwotoonemultiplexer_1_dataout}),
    .AIN({sixteentwotoonemultiplexer_2_dataout_4, sixteentwotoonemultiplexer_2_dataout_3, sixteentwotoonemultiplexer_2_dataout_2, sixteentwotoonemultiplexer_2_dataout}),
    .COUT(alsu_1_cout), .ALSUOUT(ledbar_3_p1));  // open: CIN, LSBIN, MSBIN
  // LedBar #(.inputtype("row"), .matrixcols(16)) ledbar_4: pin names not known; wires that end beside it: {ram_1_dout_4, ram_1_dout_3, ram_1_dout_2, ram_1_dout}
  Button button_2 (.out(button_2_out));
  // LedBar #(.inputtype("row"), .matrixcols(16)) ledbar_5: pin names not known; wires that end beside it: ledbar_2_p1, ledbar_5_p2
  _74175 #(.VccGndPorts("true")) u_74175_1 (
    .pin1(n74175_1_pin1), .pin2(n74175_1_pin2), .pin4(alsu_1_cout), .pin8(n74175_1_pin8[15]),
    .pin16(n74175_1_pin16), .pin9(n74175_1_pin9));  // open: pin3, pin5, pin6, pin7, pin15, pin14, pin13, pin12, pin11, pin10
  or or_2 (n74175_1_pin9, and_1_out, and_2_out);
  _74175 #(.VccGndPorts("true")) u_74175_2 (
    .pin2(n74175_2_pin2), .pin4(n74175_2_pin4), .pin8(n74175_1_pin8[15]), .pin16(n74175_1_pin16),
    .pin9(clock_1_out));  // open: pin1, pin3, pin5, pin6, pin7, pin15, pin14, pin13, pin12, pin11, pin10
  twelveBitRegLdIncrClr AR (
    .INCR(unitOfControl_arincr), .LoadActiveHigh(unitOfControl_arld), .VCC(n74175_1_pin16),
    .GND(n74175_1_pin8[15]), .CLK(clock_1_out), .BitsIN(ledbar_2_p1[11:0]),
    .BitsOUT({AR_bitsout_2[11], AR_bitsout}));  // open: ClearActiveLow, cascadeOut
  twelveBitRegLdIncrClr PC (
    .INCR(unitOfControl_pcincr), .LoadActiveHigh(unitOfControl_pcload), .VCC(n74175_1_pin16),
    .GND(n74175_1_pin8[15]), .ClearActiveLow(or_1_out), .CLK(clock_1_out), .BitsIN(ledbar_2_p1[11:0]),
    .BitsOUT(PC_bitsout));  // open: cascadeOut
  regClearLoadIncr DR (
    .INCR(unitOfControl_drincr), .LoadActiveHigh(unitOfControl_drload), .VCC(n74175_1_pin16),
    .GND(n74175_1_pin8[15]), .CLK(clock_1_out), .BitsIN(ledbar_2_p1), .BitsOUT(ledbar_5_p2));  // open: ClearActiveLow, cascadeOut
  Hex_Digit_Display hex_digit_display_9 (.value(AC_bitsout_4));  // open: dp
  Hex_Digit_Display hex_digit_display_10 (.value(AC_bitsout_3));  // open: dp
  regClearLoadIncr AC (
    .INCR(unitOfControl_acincr), .LoadActiveHigh(unitOfControl_acload), .VCC(n74175_1_pin16),
    .GND(n74175_1_pin8[15]), .ClearActiveLow(unitOfControl_acclr), .CLK(clock_1_out), .BitsIN(ledbar_3_p1),
    .BitsOUT({AC_bitsout_4, AC_bitsout_3, AC_bitsout_2, AC_bitsout}));  // open: cascadeOut
  not not_1 (n74175_1_pin1, unitOfControl_eclr);
  sixteenBitLoad IR (
    .LoadActiveHigh(unitOfControl_irld), .VCC(n74175_1_pin16), .GND(n74175_1_pin8[15]), .CLK(clock_1_out),
    .BitsIN(ledbar_2_p1), .BitsOUT(IR_bitsout));
  Hex_Digit_Display hex_digit_display_11 (.value(TR_bitsout_4));  // open: dp
  regClearLoadIncr TR (
    .LoadActiveHigh(unitOfControl_trload), .VCC(n74175_1_pin16), .GND(n74175_1_pin8[15]), .CLK(clock_1_out),
    .BitsIN(ledbar_2_p1), .BitsOUT({TR_bitsout_4, TR_bitsout_3, TR_bitsout_2, TR_bitsout}));  // open: INCR, ClearActiveLow, cascadeOut
  eightBitLoad OUTR (
    .LoadActiveHigh(unitOfControl_outrload), .VCC(n74175_1_pin16), .GND(n74175_1_pin8[15]),
    .ClearActiveLow(n74175_2_pin2), .CLK(clock_1_out), .BitsIN(ledbar_2_p1[7:0]),
    .BitsOUT({n74175_1_pin8[15], OUTR_bitsout}));  // open: cascadeOut
  // LedBar #(.inputtype("row"), .matrixcols(12)) ledbar_6: pin names not known; wires that end beside it: {AR_bitsout_2[11], AR_bitsout}
  Hex_Digit_Display hex_digit_display_12 (.value(AC_bitsout_2));  // open: dp
  Hex_Digit_Display hex_digit_display_13 (.value(AC_bitsout));  // open: dp
  and and_1 (and_1_out, unitOfControl_eclr, clock_1_out);
  and and_2 (and_2_out, unitOfControl_eload, clock_1_out);
  Hex_Digit_Display hex_digit_display_14 (.value(TR_bitsout_3));  // open: dp
  Hex_Digit_Display hex_digit_display_15 (.value(TR_bitsout_2));  // open: dp
  Hex_Digit_Display hex_digit_display_16 (.value(ram_1_dout_4));  // open: dp
  Hex_Digit_Display hex_digit_display_17 (.value(ram_1_dout_3));  // open: dp
  Hex_Digit_Display hex_digit_display_18 (.value(TR_bitsout));  // open: dp
  or or_3 (n74175_2_pin4, OUTR_bitsout[6], OUTR_bitsout[5], OUTR_bitsout[4], OUTR_bitsout[3], OUTR_bitsout[2], OUTR_bitsout[1], OUTR_bitsout[0]);
  Hex_Digit_Display hex_digit_display_19 (.value(ram_1_dout_2));  // open: dp
  Hex_Digit_Display hex_digit_display_20 (.value(ram_1_dout));  // open: dp
  Hex_Digit_Display hex_digit_display_21 (.value(PC_bitsout[11:8]));  // open: dp
  Hex_Digit_Display hex_digit_display_22 (.value(PC_bitsout[7:4]));  // open: dp
  Hex_Digit_Display hex_digit_display_23 (.value(ledbar_7_p1));  // open: dp
  // LedBar #(.inputtype("row"), .matrixcols(4)) ledbar_7: pin names not known; wires that end beside it: ledbar_7_p1
  TTY tty_1 (.data(OUTR_bitsout), .clk(clock_1_out), .we(n74175_2_pin2), .clr(button_3_out));
  Hex_Digit_Display hex_digit_display_24 (.value(PC_bitsout[3:0]));  // open: dp
  // LedBar #(.inputtype("row"), .matrixcols(16)) ledbar_8: pin names not known; wires that end beside it: IR_bitsout
  Button button_3 (.out(button_3_out));
  RAM #(.addrWidth(11), .asyncread("true"), .dataWidth(16)) ram_2 (
    .addr(AR_bitsout), .we(unitOfControl_ramwrite), .oe(unitOfControl_ramread), .clk(clock_1_out),
    .din(ledbar_2_p1), .dout(ram_2_dout));
  sixteenEightToOneMultiplexer BUSMULTIPLEXER (
    .ENActiveHigh(n74175_1_pin16), .GND(n74175_1_pin8[15]), .VCC(n74175_1_pin16), .S0(unitOfControl_bs0),
    .S1(unitOfControl_bs1), .S2(unitOfControl_bs2),
    .INPUT1({{4{n74175_1_pin8[15]}}, AR_bitsout_2[11], AR_bitsout}),
    .INPUT2({{4{n74175_1_pin8[15]}}, PC_bitsout}), .INPUT3(ledbar_5_p2),
    .INPUT4({AC_bitsout_4, AC_bitsout_3, AC_bitsout_2, AC_bitsout}), .INPUT5(IR_bitsout),
    .INPUT6({TR_bitsout_4, TR_bitsout_3, TR_bitsout_2, TR_bitsout}), .INPUT7(ram_2_dout),
    .DATAOUT(BUSMULTIPLEXER_dataout));
  sixteenEightWithZeroToOneMultiplexr sixteeneightwithzerotoonemultiplexr_1 (
    .ENActiveHigh(n74175_1_pin16), .GND(n74175_1_pin8[15]), .VCC(n74175_1_pin16), .S0(unitOfControl_bs0),
    .S1(unitOfControl_bs1), .S2(unitOfControl_bs2),
    .INPUT0({ram_1_dout_4, ram_1_dout_3, ram_1_dout_2, ram_1_dout}),
    .INPUT1({{4{n74175_1_pin8[15]}}, addressOfInterruptFunction_bitsout}),
    .DATAOUT(sixteeneightwithzerotoonemultiplexr_1_dataout));  // open: INPUT2, INPUT3, INPUT4, INPUT5, INPUT6, INPUT7
  controlUnit unitOfControl (
    .CLK(clock_1_out), .VCC(n74175_1_pin16), .GND(n74175_1_pin8[15]), .irIN(IR_bitsout),
    .bit12AR(AR_bitsout_2[11]), .ACIN({AC_bitsout_4, AC_bitsout_3, AC_bitsout_2, AC_bitsout}),
    .DRIN(ledbar_5_p2), .scCLR(or_1_out), .EFLIPFLOPIN(n74175_1_pin2),
    .inputBufferNotEmpty(keyboard_1_avail), .BS3(unitOfControl_bs3), .BS2(unitOfControl_bs2),
    .BS1(unitOfControl_bs1), .BS0(unitOfControl_bs0), .ARLD(unitOfControl_arld),
    .ROMREAD(unitOfControl_romread), .ROMWRITE(unitOfControl_romwrite), .RAMREAD(unitOfControl_ramread),
    .RAMWRITE(unitOfControl_ramwrite), .IRLD(unitOfControl_irld), .ACCLR(unitOfControl_acclr),
    .ECLR(unitOfControl_eclr), .PCINCR(unitOfControl_pcincr), .ACLOAD(unitOfControl_acload),
    .ELOAD(unitOfControl_eload), .DRLOAD(unitOfControl_drload), .ALSUS3(unitOfControl_alsus3),
    .ALSUS2(unitOfControl_alsus2), .ALSUS1(unitOfControl_alsus1), .ALSUS0(unitOfControl_alsus0),
    .MLTDRINRIN(unitOfControl_mltdrinrin), .PCLOAD(unitOfControl_pcload), .ARINCR(unitOfControl_arincr),
    .DRINCR(unitOfControl_drincr), .OUTRLOAD(unitOfControl_outrload), .sequencer(ledbar_7_p1),
    .ALSUSELECTOR(unitOfControl_alsuselector), .ACINCR(unitOfControl_acincr), .TRLOAD(unitOfControl_trload),
    .inputFlush(unitOfControl_inputflush), .LOADB9(unitOfControl_loadb9));  // open: ACCMPLMNT, ECMPLMNT, ACSHFR, ACSHFL, LOADB1, LOADB2, LOADB3, LOADB4, LOADB5, LOADB6, LOADB7, LOADB8, LOADB10, LOADB11, LOADB12, LOADB13, LOADB14, LOADB15
  twelveBitRegLdIncrClr addressOfInterruptFunction (
    .LoadActiveHigh(unitOfControl_loadb9), .VCC(n74175_1_pin16), .GND(n74175_1_pin8[15]), .CLK(clock_1_out),
    .BitsIN(ledbar_2_p1[11:0]), .BitsOUT(addressOfInterruptFunction_bitsout));  // open: INCR, ClearActiveLow, cascadeOut
  sixteenTwoToOneMultiplexer sixteentwotoonemultiplexer_4 (
    .ENActiveHigh(n74175_1_pin16), .GND(n74175_1_pin8[15]), .VCC(n74175_1_pin16), .S0(unitOfControl_bs3),
    .INPUT0(BUSMULTIPLEXER_dataout), .INPUT1(sixteeneightwithzerotoonemultiplexr_1_dataout),
    .DATAOUT(ledbar_2_p1));
  Hex_Digit_Display hex_digit_display_25 (.value(addressOfInterruptFunction_bitsout[11:8]));  // open: dp
  Hex_Digit_Display hex_digit_display_26 (.value(addressOfInterruptFunction_bitsout[7:4]));  // open: dp
  Hex_Digit_Display hex_digit_display_27 (.value(addressOfInterruptFunction_bitsout[3:0]));  // open: dp
  Hex_Digit_Display hex_digit_display_28 (.value(ledbar_2_p1[11:8]));  // open: dp
  Hex_Digit_Display hex_digit_display_29 (.value(ledbar_2_p1[7:4]));  // open: dp
  Hex_Digit_Display hex_digit_display_30 (.value(ledbar_2_p1[3:0]));  // open: dp
  // also tied to GND on the sheet: n74175_1_pin8[15]
  // also tied to VCC on the sheet: n74175_1_pin16

  // Notes on the sheet:
  //   Clear
  //   buffer not empty
  //   S0 =1 -> AIN from MLTDRINR
  //   BIN from AC
  //   MLTDRINR
  //   bit 12 will decide address is for ram or Storage
  //   NON volatile storage
  //   Bit12
  //   ECLR
  //   delay flipflop
  //   EOUT
  //   Youssef Mohamed Fathi 247349
  //   load
  //   S3
  //   S3
  //   S0
  //   S0
  //   address 8
  //   RAM
endmodule

module regClearLoadIncr (
  input  INCR,
  input  LoadActiveHigh,
  input  VCC,
  input  GND,
  input  ClearActiveLow,
  input  CLK,
  input  [15:0] BitsIN,
  output [15:0] BitsOUT,
  output cascadeOut
);

  wire n7404_1_pin2, n7404_1_pin12, n74163_1_pin15, n74163_2_pin15, n74163_3_pin15;

  _7404 u_7404_1 (
    .pin1(ClearActiveLow), .pin2(n7404_1_pin2), .pin13(LoadActiveHigh), .pin12(n7404_1_pin12));  // open: pin3, pin4, pin5, pin6, pin11, pin10, pin9, pin8
  _74163 u_74163_1 (
    .pin1(n7404_1_pin2), .pin2(CLK), .pin3(BitsIN[0]), .pin4(BitsIN[1]), .pin5(BitsIN[2]), .pin6(BitsIN[3]),
    .pin7(VCC), .pin15(n74163_1_pin15), .pin14(BitsOUT[0]), .pin13(BitsOUT[1]), .pin12(BitsOUT[2]),
    .pin11(BitsOUT[3]), .pin10(INCR), .pin9(n7404_1_pin12));
  _74163 u_74163_2 (
    .pin1(n7404_1_pin2), .pin2(CLK), .pin3(BitsIN[4]), .pin4(BitsIN[5]), .pin5(BitsIN[6]), .pin6(BitsIN[7]),
    .pin7(VCC), .pin15(n74163_2_pin15), .pin14(BitsOUT[4]), .pin13(BitsOUT[5]), .pin12(BitsOUT[6]),
    .pin11(BitsOUT[7]), .pin10(n74163_1_pin15), .pin9(n7404_1_pin12));
  _74163 u_74163_3 (
    .pin1(n7404_1_pin2), .pin2(CLK), .pin3(BitsIN[8]), .pin4(BitsIN[9]), .pin5(BitsIN[10]),
    .pin6(BitsIN[11]), .pin7(VCC), .pin15(n74163_3_pin15), .pin14(BitsOUT[8]), .pin13(BitsOUT[9]),
    .pin12(BitsOUT[10]), .pin11(BitsOUT[11]), .pin10(n74163_2_pin15), .pin9(n7404_1_pin12));
  _74163 u_74163_4 (
    .pin1(n7404_1_pin2), .pin2(CLK), .pin3(BitsIN[12]), .pin4(BitsIN[13]), .pin5(BitsIN[14]),
    .pin6(BitsIN[15]), .pin7(VCC), .pin15(cascadeOut), .pin14(BitsOUT[12]), .pin13(BitsOUT[13]),
    .pin12(BitsOUT[14]), .pin11(BitsOUT[15]), .pin10(n74163_3_pin15), .pin9(n7404_1_pin12));

  // Notes on the sheet:
  //   clear
  //   active high
  //   load
  //   active high
  //   clock
  //   enable count
  //   ENP
endmodule

module twelveBitRegLdIncrClr (
  input  INCR,
  input  LoadActiveHigh,
  input  VCC,
  input  GND,
  input  ClearActiveLow,
  input  CLK,
  input  [11:0] BitsIN,
  output [11:0] BitsOUT,
  output cascadeOut
);

  wire n7404_1_pin2, n7404_1_pin12, n74163_1_pin15, n74163_2_pin15;

  _7404 u_7404_1 (
    .pin1(ClearActiveLow), .pin2(n7404_1_pin2), .pin13(LoadActiveHigh), .pin12(n7404_1_pin12));  // open: pin3, pin4, pin5, pin6, pin11, pin10, pin9, pin8
  _74163 u_74163_1 (
    .pin1(n7404_1_pin2), .pin2(CLK), .pin3(BitsIN[0]), .pin4(BitsIN[1]), .pin5(BitsIN[2]), .pin6(BitsIN[3]),
    .pin7(VCC), .pin15(n74163_1_pin15), .pin14(BitsOUT[0]), .pin13(BitsOUT[1]), .pin12(BitsOUT[2]),
    .pin11(BitsOUT[3]), .pin10(INCR), .pin9(n7404_1_pin12));
  _74163 u_74163_2 (
    .pin1(n7404_1_pin2), .pin2(CLK), .pin3(BitsIN[4]), .pin4(BitsIN[5]), .pin5(BitsIN[6]), .pin6(BitsIN[7]),
    .pin7(VCC), .pin15(n74163_2_pin15), .pin14(BitsOUT[4]), .pin13(BitsOUT[5]), .pin12(BitsOUT[6]),
    .pin11(BitsOUT[7]), .pin10(n74163_1_pin15), .pin9(n7404_1_pin12));
  _74163 u_74163_3 (
    .pin1(n7404_1_pin2), .pin2(CLK), .pin3(BitsIN[8]), .pin4(BitsIN[9]), .pin5(BitsIN[10]),
    .pin6(BitsIN[11]), .pin7(VCC), .pin15(cascadeOut), .pin14(BitsOUT[8]), .pin13(BitsOUT[9]),
    .pin12(BitsOUT[10]), .pin11(BitsOUT[11]), .pin10(n74163_2_pin15), .pin9(n7404_1_pin12));

  // Notes on the sheet:
  //   clear
  //   active high
  //   load
  //   active high
  //   clock
  //   enable count
endmodule

module sixteenBitLoad (
  input  LoadActiveHigh,
  input  VCC,
  input  GND,
  input  CLK,
  input  [15:0] BitsIN,
  output [15:0] BitsOUT
);

  wire n7404_1_pin1, n7404_1_pin2, n7404_1_pin12, n74163_1_pin10, n74163_1_pin15, n74163_2_pin15,
       n74163_3_pin15, n74163_4_pin15;

  _7404 u_7404_1 (
    .pin1(n7404_1_pin1), .pin2(n7404_1_pin2), .pin13(LoadActiveHigh), .pin12(n7404_1_pin12));  // open: pin3, pin4, pin5, pin6, pin11, pin10, pin9, pin8
  _74163 u_74163_1 (
    .pin1(n7404_1_pin2), .pin2(CLK), .pin3(BitsIN[0]), .pin4(BitsIN[1]), .pin5(BitsIN[2]), .pin6(BitsIN[3]),
    .pin7(VCC), .pin15(n74163_1_pin15), .pin14(BitsOUT[0]), .pin13(BitsOUT[1]), .pin12(BitsOUT[2]),
    .pin11(BitsOUT[3]), .pin10(n74163_1_pin10), .pin9(n7404_1_pin12));
  _74163 u_74163_2 (
    .pin1(n7404_1_pin2), .pin2(CLK), .pin3(BitsIN[4]), .pin4(BitsIN[5]), .pin5(BitsIN[6]), .pin6(BitsIN[7]),
    .pin7(VCC), .pin15(n74163_2_pin15), .pin14(BitsOUT[4]), .pin13(BitsOUT[5]), .pin12(BitsOUT[6]),
    .pin11(BitsOUT[7]), .pin10(n74163_1_pin15), .pin9(n7404_1_pin12));
  _74163 u_74163_3 (
    .pin1(n7404_1_pin2), .pin2(CLK), .pin3(BitsIN[8]), .pin4(BitsIN[9]), .pin5(BitsIN[10]),
    .pin6(BitsIN[11]), .pin7(VCC), .pin15(n74163_3_pin15), .pin14(BitsOUT[8]), .pin13(BitsOUT[9]),
    .pin12(BitsOUT[10]), .pin11(BitsOUT[11]), .pin10(n74163_2_pin15), .pin9(n7404_1_pin12));
  _74163 u_74163_4 (
    .pin1(n7404_1_pin2), .pin2(CLK), .pin3(BitsIN[12]), .pin4(BitsIN[13]), .pin5(BitsIN[14]),
    .pin6(BitsIN[15]), .pin7(VCC), .pin15(n74163_4_pin15), .pin14(BitsOUT[12]), .pin13(BitsOUT[13]),
    .pin12(BitsOUT[14]), .pin11(BitsOUT[15]), .pin10(n74163_3_pin15), .pin9(n7404_1_pin12));
  // also tied to GND on the sheet: {n7404_1_pin1, n74163_1_pin10}

  // Notes on the sheet:
  //   clear
  //   active high
  //   load
  //   active high
  //   clock
  //   enable count
  //   ENP
endmodule

module eightBitLoad (
  input  LoadActiveHigh,
  input  VCC,
  input  GND,
  input  ClearActiveLow,
  input  CLK,
  input  [7:0] BitsIN,
  output [7:0] BitsOUT,
  output cascadeOut
);

  wire n7404_1_pin2, n7404_1_pin12, n74163_1_pin10, n74163_1_pin15;

  _7404 u_7404_1 (
    .pin1(ClearActiveLow), .pin2(n7404_1_pin2), .pin13(LoadActiveHigh), .pin12(n7404_1_pin12));  // open: pin3, pin4, pin5, pin6, pin11, pin10, pin9, pin8
  _74163 u_74163_1 (
    .pin1(n7404_1_pin2), .pin2(CLK), .pin3(BitsIN[0]), .pin4(BitsIN[1]), .pin5(BitsIN[2]), .pin6(BitsIN[3]),
    .pin7(VCC), .pin15(n74163_1_pin15), .pin14(BitsOUT[0]), .pin13(BitsOUT[1]), .pin12(BitsOUT[2]),
    .pin11(BitsOUT[3]), .pin10(n74163_1_pin10), .pin9(n7404_1_pin12));
  _74163 u_74163_2 (
    .pin1(n7404_1_pin2), .pin2(CLK), .pin3(BitsIN[4]), .pin4(BitsIN[5]), .pin5(BitsIN[6]), .pin6(BitsIN[7]),
    .pin7(VCC), .pin15(cascadeOut), .pin14(BitsOUT[4]), .pin13(BitsOUT[5]), .pin12(BitsOUT[6]),
    .pin11(BitsOUT[7]), .pin10(n74163_1_pin15), .pin9(n7404_1_pin12));
  // also tied to GND on the sheet: n74163_1_pin10

  // Notes on the sheet:
  //   clear
  //   active high
  //   load
  //   active high
  //   clock
  //   enable count
endmodule

module sixteenEightToOneMultiplexer (
  input  ENActiveHigh,
  input  GND,
  input  VCC,
  input  S0,
  input  S1,
  input  S2,
  input  [15:0] INPUT1,
  input  [15:0] INPUT2,
  input  [15:0] INPUT3,
  input  [15:0] INPUT4,
  input  [15:0] INPUT5,
  input  [15:0] INPUT6,
  input  [15:0] INPUT7,
  output [15:0] DATAOUT
);

  wire n74151_1_pin7;

  _74151 #(.VccGndPorts("true")) u_74151_1 (
    .pin1(INPUT3[12]), .pin2(INPUT2[12]), .pin3(INPUT1[12]), .pin5(DATAOUT[12]), .pin7(n74151_1_pin7),
    .pin8(GND), .pin16(VCC), .pin15(INPUT4[12]), .pin14(INPUT5[12]), .pin13(INPUT6[12]), .pin12(INPUT7[12]),
    .pin11(S0), .pin10(S1), .pin9(S2));  // open: pin4, pin6
  _74151 #(.VccGndPorts("true")) u_74151_2 (
    .pin1(INPUT3[13]), .pin2(INPUT2[13]), .pin3(INPUT1[13]), .pin5(DATAOUT[13]), .pin7(n74151_1_pin7),
    .pin8(GND), .pin16(VCC), .pin15(INPUT4[13]), .pin14(INPUT5[13]), .pin13(INPUT6[13]), .pin12(INPUT7[13]),
    .pin11(S0), .pin10(S1), .pin9(S2));  // open: pin4, pin6
  _74151 #(.VccGndPorts("true")) u_74151_3 (
    .pin1(INPUT3[14]), .pin2(INPUT2[14]), .pin3(INPUT1[14]), .pin5(DATAOUT[14]), .pin7(n74151_1_pin7),
    .pin8(GND), .pin16(VCC), .pin15(INPUT4[14]), .pin14(INPUT5[14]), .pin13(INPUT6[14]), .pin12(INPUT7[14]),
    .pin11(S0), .pin10(S1), .pin9(S2));  // open: pin4, pin6
  _74151 #(.VccGndPorts("true")) u_74151_4 (
    .pin1(INPUT3[15]), .pin2(INPUT2[15]), .pin3(INPUT1[15]), .pin5(DATAOUT[15]), .pin7(n74151_1_pin7),
    .pin8(GND), .pin16(VCC), .pin15(INPUT4[15]), .pin14(INPUT5[15]), .pin13(INPUT6[15]), .pin12(INPUT7[15]),
    .pin11(S0), .pin10(S1), .pin9(S2));  // open: pin4, pin6
  _74151 #(.VccGndPorts("true")) u_74151_5 (
    .pin1(INPUT3[2]), .pin2(INPUT2[2]), .pin3(INPUT1[2]), .pin5(DATAOUT[2]), .pin7(n74151_1_pin7),
    .pin8(GND), .pin16(VCC), .pin15(INPUT4[2]), .pin14(INPUT5[2]), .pin13(INPUT6[2]), .pin12(INPUT7[2]),
    .pin11(S0), .pin10(S1), .pin9(S2));  // open: pin4, pin6
  _74151 #(.VccGndPorts("true")) u_74151_6 (
    .pin1(INPUT3[3]), .pin2(INPUT2[3]), .pin3(INPUT1[3]), .pin5(DATAOUT[3]), .pin7(n74151_1_pin7),
    .pin8(GND), .pin16(VCC), .pin15(INPUT4[3]), .pin14(INPUT5[3]), .pin13(INPUT6[3]), .pin12(INPUT7[3]),
    .pin11(S0), .pin10(S1), .pin9(S2));  // open: pin4, pin6
  _74151 #(.VccGndPorts("true")) u_74151_7 (
    .pin1(INPUT3[4]), .pin2(INPUT2[4]), .pin3(INPUT1[4]), .pin5(DATAOUT[4]), .pin7(n74151_1_pin7),
    .pin8(GND), .pin16(VCC), .pin15(INPUT4[4]), .pin14(INPUT5[4]), .pin13(INPUT6[4]), .pin12(INPUT7[4]),
    .pin11(S0), .pin10(S1), .pin9(S2));  // open: pin4, pin6
  _74151 #(.VccGndPorts("true")) u_74151_8 (
    .pin1(INPUT3[5]), .pin2(INPUT2[5]), .pin3(INPUT1[5]), .pin5(DATAOUT[5]), .pin7(n74151_1_pin7),
    .pin8(GND), .pin16(VCC), .pin15(INPUT4[5]), .pin14(INPUT5[5]), .pin13(INPUT6[5]), .pin12(INPUT7[5]),
    .pin11(S0), .pin10(S1), .pin9(S2));  // open: pin4, pin6
  _74151 #(.VccGndPorts("true")) u_74151_9 (
    .pin1(INPUT3[6]), .pin2(INPUT2[6]), .pin3(INPUT1[6]), .pin5(DATAOUT[6]), .pin7(n74151_1_pin7),
    .pin8(GND), .pin16(VCC), .pin15(INPUT4[6]), .pin14(INPUT5[6]), .pin13(INPUT6[6]), .pin12(INPUT7[6]),
    .pin11(S0), .pin10(S1), .pin9(S2));  // open: pin4, pin6
  _74151 #(.VccGndPorts("true")) u_74151_10 (
    .pin1(INPUT3[7]), .pin2(INPUT2[7]), .pin3(INPUT1[7]), .pin5(DATAOUT[7]), .pin7(n74151_1_pin7),
    .pin8(GND), .pin16(VCC), .pin15(INPUT4[7]), .pin14(INPUT5[7]), .pin13(INPUT6[7]), .pin12(INPUT7[7]),
    .pin11(S0), .pin10(S1), .pin9(S2));  // open: pin4, pin6
  _74151 #(.VccGndPorts("true")) u_74151_11 (
    .pin1(INPUT3[8]), .pin2(INPUT2[8]), .pin3(INPUT1[8]), .pin5(DATAOUT[8]), .pin7(n74151_1_pin7),
    .pin8(GND), .pin16(VCC), .pin15(INPUT4[8]), .pin14(INPUT5[8]), .pin13(INPUT6[8]), .pin12(INPUT7[8]),
    .pin11(S0), .pin10(S1), .pin9(S2));  // open: pin4, pin6
  _74151 #(.VccGndPorts("true")) u_74151_12 (
    .pin1(INPUT3[9]), .pin2(INPUT2[9]), .pin3(INPUT1[9]), .pin5(DATAOUT[9]), .pin7(n74151_1_pin7),
    .pin8(GND), .pin16(VCC), .pin15(INPUT4[9]), .pin14(INPUT5[9]), .pin13(INPUT6[9]), .pin12(INPUT7[9]),
    .pin11(S0), .pin10(S1), .pin9(S2));  // open: pin4, pin6
  _74151 #(.VccGndPorts("true")) u_74151_13 (
    .pin1(INPUT3[10]), .pin2(INPUT2[10]), .pin3(INPUT1[10]), .pin5(DATAOUT[10]), .pin7(n74151_1_pin7),
    .pin8(GND), .pin16(VCC), .pin15(INPUT4[10]), .pin14(INPUT5[10]), .pin13(INPUT6[10]), .pin12(INPUT7[10]),
    .pin11(S0), .pin10(S1), .pin9(S2));  // open: pin4, pin6
  _74151 #(.VccGndPorts("true")) u_74151_14 (
    .pin1(INPUT3[11]), .pin2(INPUT2[11]), .pin3(INPUT1[11]), .pin5(DATAOUT[11]), .pin7(n74151_1_pin7),
    .pin8(GND), .pin16(VCC), .pin15(INPUT4[11]), .pin14(INPUT5[11]), .pin13(INPUT6[11]), .pin12(INPUT7[11]),
    .pin11(S0), .pin10(S1), .pin9(S2));  // open: pin4, pin6
  _74151 #(.VccGndPorts("true")) u_74151_15 (
    .pin1(INPUT3[0]), .pin2(INPUT2[0]), .pin3(INPUT1[0]), .pin5(DATAOUT[0]), .pin7(n74151_1_pin7),
    .pin8(GND), .pin16(VCC), .pin15(INPUT4[0]), .pin14(INPUT5[0]), .pin13(INPUT6[0]), .pin12(INPUT7[0]),
    .pin11(S0), .pin10(S1), .pin9(S2));  // open: pin4, pin6
  _74151 #(.VccGndPorts("true")) u_74151_16 (
    .pin1(INPUT3[1]), .pin2(INPUT2[1]), .pin3(INPUT1[1]), .pin5(DATAOUT[1]), .pin7(n74151_1_pin7),
    .pin8(GND), .pin16(VCC), .pin15(INPUT4[1]), .pin14(INPUT5[1]), .pin13(INPUT6[1]), .pin12(INPUT7[1]),
    .pin11(S0), .pin10(S1), .pin9(S2));  // open: pin4, pin6
  not not_1 (n74151_1_pin7, ENActiveHigh);

  // Notes on the sheet:
  //   VCC
  //   INPUT7
  //   INPUT6
  //   INPUT5
  //   INPUT4
  //   INPUT3
  //   INPUT2
  //   INPUT1
  //   GND
  //   OUT
endmodule

module sixteenEightWithZeroToOneMultiplexr (
  input  ENActiveHigh,
  input  GND,
  input  VCC,
  input  S0,
  input  S1,
  input  S2,
  input  [15:0] INPUT0,
  input  [15:0] INPUT1,
  input  [15:0] INPUT2,
  input  [15:0] INPUT3,
  input  [15:0] INPUT4,
  input  [15:0] INPUT5,
  input  [15:0] INPUT6,
  input  [15:0] INPUT7,
  output [15:0] DATAOUT
);

  wire n74151_1_pin7;

  _74151 #(.VccGndPorts("true")) u_74151_1 (
    .pin1(INPUT3[12]), .pin2(INPUT2[12]), .pin3(INPUT1[12]), .pin4(INPUT0[12]), .pin5(DATAOUT[12]),
    .pin7(n74151_1_pin7), .pin8(GND), .pin16(VCC), .pin15(INPUT4[12]), .pin14(INPUT5[12]),
    .pin13(INPUT6[12]), .pin12(INPUT7[12]), .pin11(S0), .pin10(S1), .pin9(S2));  // open: pin6
  _74151 #(.VccGndPorts("true")) u_74151_2 (
    .pin1(INPUT3[13]), .pin2(INPUT2[13]), .pin3(INPUT1[13]), .pin4(INPUT0[13]), .pin5(DATAOUT[13]),
    .pin7(n74151_1_pin7), .pin8(GND), .pin16(VCC), .pin15(INPUT4[13]), .pin14(INPUT5[13]),
    .pin13(INPUT6[13]), .pin12(INPUT7[13]), .pin11(S0), .pin10(S1), .pin9(S2));  // open: pin6
  _74151 #(.VccGndPorts("true")) u_74151_3 (
    .pin1(INPUT3[14]), .pin2(INPUT2[14]), .pin3(INPUT1[14]), .pin4(INPUT0[14]), .pin5(DATAOUT[14]),
    .pin7(n74151_1_pin7), .pin8(GND), .pin16(VCC), .pin15(INPUT4[14]), .pin14(INPUT5[14]),
    .pin13(INPUT6[14]), .pin12(INPUT7[14]), .pin11(S0), .pin10(S1), .pin9(S2));  // open: pin6
  _74151 #(.VccGndPorts("true")) u_74151_4 (
    .pin1(INPUT3[15]), .pin2(INPUT2[15]), .pin3(INPUT1[15]), .pin4(INPUT0[15]), .pin5(DATAOUT[15]),
    .pin7(n74151_1_pin7), .pin8(GND), .pin16(VCC), .pin15(INPUT4[15]), .pin14(INPUT5[15]),
    .pin13(INPUT6[15]), .pin12(INPUT7[15]), .pin11(S0), .pin10(S1), .pin9(S2));  // open: pin6
  _74151 #(.VccGndPorts("true")) u_74151_5 (
    .pin1(INPUT3[2]), .pin2(INPUT2[2]), .pin3(INPUT1[2]), .pin4(INPUT0[2]), .pin5(DATAOUT[2]),
    .pin7(n74151_1_pin7), .pin8(GND), .pin16(VCC), .pin15(INPUT4[2]), .pin14(INPUT5[2]), .pin13(INPUT6[2]),
    .pin12(INPUT7[2]), .pin11(S0), .pin10(S1), .pin9(S2));  // open: pin6
  _74151 #(.VccGndPorts("true")) u_74151_6 (
    .pin1(INPUT3[3]), .pin2(INPUT2[3]), .pin3(INPUT1[3]), .pin4(INPUT0[3]), .pin5(DATAOUT[3]),
    .pin7(n74151_1_pin7), .pin8(GND), .pin16(VCC), .pin15(INPUT4[3]), .pin14(INPUT5[3]), .pin13(INPUT6[3]),
    .pin12(INPUT7[3]), .pin11(S0), .pin10(S1), .pin9(S2));  // open: pin6
  _74151 #(.VccGndPorts("true")) u_74151_7 (
    .pin1(INPUT3[4]), .pin2(INPUT2[4]), .pin3(INPUT1[4]), .pin4(INPUT0[4]), .pin5(DATAOUT[4]),
    .pin7(n74151_1_pin7), .pin8(GND), .pin16(VCC), .pin15(INPUT4[4]), .pin14(INPUT5[4]), .pin13(INPUT6[4]),
    .pin12(INPUT7[4]), .pin11(S0), .pin10(S1), .pin9(S2));  // open: pin6
  _74151 #(.VccGndPorts("true")) u_74151_8 (
    .pin1(INPUT3[5]), .pin2(INPUT2[5]), .pin3(INPUT1[5]), .pin4(INPUT0[5]), .pin5(DATAOUT[5]),
    .pin7(n74151_1_pin7), .pin8(GND), .pin16(VCC), .pin15(INPUT4[5]), .pin14(INPUT5[5]), .pin13(INPUT6[5]),
    .pin12(INPUT7[5]), .pin11(S0), .pin10(S1), .pin9(S2));  // open: pin6
  _74151 #(.VccGndPorts("true")) u_74151_9 (
    .pin1(INPUT3[6]), .pin2(INPUT2[6]), .pin3(INPUT1[6]), .pin4(INPUT0[6]), .pin5(DATAOUT[6]),
    .pin7(n74151_1_pin7), .pin8(GND), .pin16(VCC), .pin15(INPUT4[6]), .pin14(INPUT5[6]), .pin13(INPUT6[6]),
    .pin12(INPUT7[6]), .pin11(S0), .pin10(S1), .pin9(S2));  // open: pin6
  _74151 #(.VccGndPorts("true")) u_74151_10 (
    .pin1(INPUT3[7]), .pin2(INPUT2[7]), .pin3(INPUT1[7]), .pin4(INPUT0[7]), .pin5(DATAOUT[7]),
    .pin7(n74151_1_pin7), .pin8(GND), .pin16(VCC), .pin15(INPUT4[7]), .pin14(INPUT5[7]), .pin13(INPUT6[7]),
    .pin12(INPUT7[7]), .pin11(S0), .pin10(S1), .pin9(S2));  // open: pin6
  _74151 #(.VccGndPorts("true")) u_74151_11 (
    .pin1(INPUT3[8]), .pin2(INPUT2[8]), .pin3(INPUT1[8]), .pin4(INPUT0[8]), .pin5(DATAOUT[8]),
    .pin7(n74151_1_pin7), .pin8(GND), .pin16(VCC), .pin15(INPUT4[8]), .pin14(INPUT5[8]), .pin13(INPUT6[8]),
    .pin12(INPUT7[8]), .pin11(S0), .pin10(S1), .pin9(S2));  // open: pin6
  _74151 #(.VccGndPorts("true")) u_74151_12 (
    .pin1(INPUT3[9]), .pin2(INPUT2[9]), .pin3(INPUT1[9]), .pin4(INPUT0[9]), .pin5(DATAOUT[9]),
    .pin7(n74151_1_pin7), .pin8(GND), .pin16(VCC), .pin15(INPUT4[9]), .pin14(INPUT5[9]), .pin13(INPUT6[9]),
    .pin12(INPUT7[9]), .pin11(S0), .pin10(S1), .pin9(S2));  // open: pin6
  _74151 #(.VccGndPorts("true")) u_74151_13 (
    .pin1(INPUT3[10]), .pin2(INPUT2[10]), .pin3(INPUT1[10]), .pin4(INPUT0[10]), .pin5(DATAOUT[10]),
    .pin7(n74151_1_pin7), .pin8(GND), .pin16(VCC), .pin15(INPUT4[10]), .pin14(INPUT5[10]),
    .pin13(INPUT6[10]), .pin12(INPUT7[10]), .pin11(S0), .pin10(S1), .pin9(S2));  // open: pin6
  _74151 #(.VccGndPorts("true")) u_74151_14 (
    .pin1(INPUT3[11]), .pin2(INPUT2[11]), .pin3(INPUT1[11]), .pin4(INPUT0[11]), .pin5(DATAOUT[11]),
    .pin7(n74151_1_pin7), .pin8(GND), .pin16(VCC), .pin15(INPUT4[11]), .pin14(INPUT5[11]),
    .pin13(INPUT6[11]), .pin12(INPUT7[11]), .pin11(S0), .pin10(S1), .pin9(S2));  // open: pin6
  _74151 #(.VccGndPorts("true")) u_74151_15 (
    .pin1(INPUT3[0]), .pin2(INPUT2[0]), .pin3(INPUT1[0]), .pin4(INPUT0[0]), .pin5(DATAOUT[0]),
    .pin7(n74151_1_pin7), .pin8(GND), .pin16(VCC), .pin15(INPUT4[0]), .pin14(INPUT5[0]), .pin13(INPUT6[0]),
    .pin12(INPUT7[0]), .pin11(S0), .pin10(S1), .pin9(S2));  // open: pin6
  _74151 #(.VccGndPorts("true")) u_74151_16 (
    .pin1(INPUT3[1]), .pin2(INPUT2[1]), .pin3(INPUT1[1]), .pin4(INPUT0[1]), .pin5(DATAOUT[1]),
    .pin7(n74151_1_pin7), .pin8(GND), .pin16(VCC), .pin15(INPUT4[1]), .pin14(INPUT5[1]), .pin13(INPUT6[1]),
    .pin12(INPUT7[1]), .pin11(S0), .pin10(S1), .pin9(S2));  // open: pin6
  not not_1 (n74151_1_pin7, ENActiveHigh);

  // Notes on the sheet:
  //   INPUT0
  //   VCC
  //   INPUT7
  //   INPUT6
  //   INPUT5
  //   INPUT4
  //   INPUT3
  //   INPUT2
  //   INPUT1
  //   GND
  //   OUT
endmodule

module ORARRAY (
  input  [15:0] IN2,
  input  [15:0] IN1,
  input  VCC,
  input  GND,
  output [15:0] OUTOR
);

  _7432 #(.VccGndPorts("true")) u_7432_1 (
    .pin1(IN1[2]), .pin2(IN2[2]), .pin3(OUTOR[2]), .pin4(IN1[3]), .pin5(IN2[3]), .pin6(OUTOR[3]), .pin7(GND),
    .pin14(VCC), .pin13(IN1[0]), .pin12(IN2[0]), .pin11(OUTOR[0]), .pin10(IN1[1]), .pin9(IN2[1]),
    .pin8(OUTOR[1]));
  _7432 #(.VccGndPorts("true")) u_7432_2 (
    .pin1(IN1[6]), .pin2(IN2[6]), .pin3(OUTOR[6]), .pin4(IN1[7]), .pin5(IN2[7]), .pin6(OUTOR[7]), .pin7(GND),
    .pin14(VCC), .pin13(IN1[4]), .pin12(IN2[4]), .pin11(OUTOR[4]), .pin10(IN1[5]), .pin9(IN2[5]),
    .pin8(OUTOR[5]));
  _7432 #(.VccGndPorts("true")) u_7432_3 (
    .pin1(IN1[10]), .pin2(IN2[10]), .pin3(OUTOR[10]), .pin4(IN1[11]), .pin5(IN2[11]), .pin6(OUTOR[11]),
    .pin7(GND), .pin14(VCC), .pin13(IN1[8]), .pin12(IN2[8]), .pin11(OUTOR[8]), .pin10(IN1[9]), .pin9(IN2[9]),
    .pin8(OUTOR[9]));
  _7432 #(.VccGndPorts("true")) u_7432_4 (
    .pin1(IN1[14]), .pin2(IN2[14]), .pin3(OUTOR[14]), .pin4(IN1[15]), .pin5(IN2[15]), .pin6(OUTOR[15]),
    .pin7(GND), .pin14(VCC), .pin13(IN1[12]), .pin12(IN2[12]), .pin11(OUTOR[12]), .pin10(IN1[13]),
    .pin9(IN2[13]), .pin8(OUTOR[13]));

  // Notes on the sheet:
  //   IN1
  //   IN2
  //   OUT
endmodule

module testCir (
);

  wire alsu_1_cout, button_1_out, clock_1_out, dipswitch_2_p1, dipswitch_3_p1, dipswitch_3_p2,
       dipswitch_3_p3, dipswitch_3_p4, dipswitch_3_p5, dipswitch_4_p1, dipswitch_4_p2;
  wire [15:0] alsu_1_alsuout, regclearloadincr_1_bitsout, undriven, undriven_2, undriven_3;

  Clock clock_1 (.out(clock_1_out));
  // DipSwitch #(.number(16)) dipswitch_1: pin names not known
  Button button_1 (.out(button_1_out));
  // DipSwitch #(.number(16)) dipswitch_2: pin names not known; wires that end beside it: dipswitch_2_p1
  // DipSwitch #(.number(5)) dipswitch_3: pin names not known; wires that end beside it: dipswitch_3_p1, dipswitch_3_p2, dipswitch_3_p3, dipswitch_3_p4, dipswitch_3_p5
  // DipSwitch #(.number(2)) dipswitch_4: pin names not known; wires that end beside it: dipswitch_4_p1, dipswitch_4_p2
  LedBar #(.matrixcols(16)) ledbar_1 (
    .led0(regclearloadincr_1_bitsout[15]), .led1(regclearloadincr_1_bitsout[14]),
    .led2(regclearloadincr_1_bitsout[13]), .led3(regclearloadincr_1_bitsout[12]),
    .led4(regclearloadincr_1_bitsout[11]), .led5(regclearloadincr_1_bitsout[10]),
    .led6(regclearloadincr_1_bitsout[9]), .led7(regclearloadincr_1_bitsout[8]),
    .led8(regclearloadincr_1_bitsout[7]), .led9(regclearloadincr_1_bitsout[6]),
    .led10(regclearloadincr_1_bitsout[5]), .led11(regclearloadincr_1_bitsout[4]),
    .led12(regclearloadincr_1_bitsout[3]), .led13(regclearloadincr_1_bitsout[2]),
    .led14(regclearloadincr_1_bitsout[1]), .led15(regclearloadincr_1_bitsout[0]));
  regClearLoadIncr regclearloadincr_1 (
    .INCR(button_1_out), .LoadActiveHigh(dipswitch_2_p1), .VCC(1'b1), .GND(1'b0), .CLK(clock_1_out),
    .BitsOUT(regclearloadincr_1_bitsout));  // open: ClearActiveLow, BitsIN, cascadeOut
  ALSU alsu_1 (
    .VCC(1'b1), .GND(1'b0), .S3(dipswitch_3_p1), .S2(dipswitch_3_p2), .S1(dipswitch_3_p3),
    .S0(dipswitch_3_p4), .CIN(dipswitch_3_p5), .BIN(undriven_2), .AIN(undriven), .LSBIN(dipswitch_4_p1),
    .MSBIN(dipswitch_4_p2), .COUT(alsu_1_cout), .ALSUOUT(alsu_1_alsuout));
  LedBar #(.matrixcols(16)) ledbar_2 (
    .led0(undriven_3[15]), .led1(undriven_3[14]), .led2(undriven_3[13]), .led3(undriven_3[12]),
    .led4(undriven_3[11]), .led5(undriven_3[10]), .led6(undriven_3[9]), .led7(undriven_3[8]),
    .led8(undriven_3[7]), .led9(undriven_3[6]), .led10(undriven_3[5]), .led11(undriven_3[4]),
    .led12(undriven_3[3]), .led13(undriven_3[2]), .led14(undriven_3[1]), .led15(undriven_3[0]));
endmodule

module sixteenTwoToOneMultiplexer (
  input  ENActiveHigh,
  input  GND,
  input  VCC,
  input  S0,
  input  [15:0] INPUT0,
  input  [15:0] INPUT1,
  output [15:0] DATAOUT
);

  wire n74151_1_pin7, n74151_1_pin9, n74151_1_pin10;
  wire [15:0] n74151_15_pin1, n74151_15_pin2, n74151_15_pin12, n74151_15_pin13, n74151_15_pin14,
       n74151_15_pin15;

  _74151 #(.VccGndPorts("true")) u_74151_1 (
    .pin1(n74151_15_pin1[12]), .pin2(n74151_15_pin2[12]), .pin3(INPUT1[12]), .pin4(INPUT0[12]),
    .pin5(DATAOUT[12]), .pin7(n74151_1_pin7), .pin8(GND), .pin16(VCC), .pin15(n74151_15_pin15[12]),
    .pin14(n74151_15_pin14[12]), .pin13(n74151_15_pin13[12]), .pin12(n74151_15_pin12[12]), .pin11(S0),
    .pin10(n74151_1_pin10), .pin9(n74151_1_pin9));  // open: pin6
  _74151 #(.VccGndPorts("true")) u_74151_2 (
    .pin1(n74151_15_pin1[13]), .pin2(n74151_15_pin2[13]), .pin3(INPUT1[13]), .pin4(INPUT0[13]),
    .pin5(DATAOUT[13]), .pin7(n74151_1_pin7), .pin8(GND), .pin16(VCC), .pin15(n74151_15_pin15[13]),
    .pin14(n74151_15_pin14[13]), .pin13(n74151_15_pin13[13]), .pin12(n74151_15_pin12[13]), .pin11(S0),
    .pin10(n74151_1_pin10), .pin9(n74151_1_pin9));  // open: pin6
  _74151 #(.VccGndPorts("true")) u_74151_3 (
    .pin1(n74151_15_pin1[14]), .pin2(n74151_15_pin2[14]), .pin3(INPUT1[14]), .pin4(INPUT0[14]),
    .pin5(DATAOUT[14]), .pin7(n74151_1_pin7), .pin8(GND), .pin16(VCC), .pin15(n74151_15_pin15[14]),
    .pin14(n74151_15_pin14[14]), .pin13(n74151_15_pin13[14]), .pin12(n74151_15_pin12[14]), .pin11(S0),
    .pin10(n74151_1_pin10), .pin9(n74151_1_pin9));  // open: pin6
  _74151 #(.VccGndPorts("true")) u_74151_4 (
    .pin1(n74151_15_pin1[15]), .pin2(n74151_15_pin2[15]), .pin3(INPUT1[15]), .pin4(INPUT0[15]),
    .pin5(DATAOUT[15]), .pin7(n74151_1_pin7), .pin8(GND), .pin16(VCC), .pin15(n74151_15_pin15[15]),
    .pin14(n74151_15_pin14[15]), .pin13(n74151_15_pin13[15]), .pin12(n74151_15_pin12[15]), .pin11(S0),
    .pin10(n74151_1_pin10), .pin9(n74151_1_pin9));  // open: pin6
  _74151 #(.VccGndPorts("true")) u_74151_5 (
    .pin1(n74151_15_pin1[2]), .pin2(n74151_15_pin2[2]), .pin3(INPUT1[2]), .pin4(INPUT0[2]),
    .pin5(DATAOUT[2]), .pin7(n74151_1_pin7), .pin8(GND), .pin16(VCC), .pin15(n74151_15_pin15[2]),
    .pin14(n74151_15_pin14[2]), .pin13(n74151_15_pin13[2]), .pin12(n74151_15_pin12[2]), .pin11(S0),
    .pin10(n74151_1_pin10), .pin9(n74151_1_pin9));  // open: pin6
  _74151 #(.VccGndPorts("true")) u_74151_6 (
    .pin1(n74151_15_pin1[3]), .pin2(n74151_15_pin2[3]), .pin3(INPUT1[3]), .pin4(INPUT0[3]),
    .pin5(DATAOUT[3]), .pin7(n74151_1_pin7), .pin8(GND), .pin16(VCC), .pin15(n74151_15_pin15[3]),
    .pin14(n74151_15_pin14[3]), .pin13(n74151_15_pin13[3]), .pin12(n74151_15_pin12[3]), .pin11(S0),
    .pin10(n74151_1_pin10), .pin9(n74151_1_pin9));  // open: pin6
  _74151 #(.VccGndPorts("true")) u_74151_7 (
    .pin1(n74151_15_pin1[4]), .pin2(n74151_15_pin2[4]), .pin3(INPUT1[4]), .pin4(INPUT0[4]),
    .pin5(DATAOUT[4]), .pin7(n74151_1_pin7), .pin8(GND), .pin16(VCC), .pin15(n74151_15_pin15[4]),
    .pin14(n74151_15_pin14[4]), .pin13(n74151_15_pin13[4]), .pin12(n74151_15_pin12[4]), .pin11(S0),
    .pin10(n74151_1_pin10), .pin9(n74151_1_pin9));  // open: pin6
  _74151 #(.VccGndPorts("true")) u_74151_8 (
    .pin1(n74151_15_pin1[5]), .pin2(n74151_15_pin2[5]), .pin3(INPUT1[5]), .pin4(INPUT0[5]),
    .pin5(DATAOUT[5]), .pin7(n74151_1_pin7), .pin8(GND), .pin16(VCC), .pin15(n74151_15_pin15[5]),
    .pin14(n74151_15_pin14[5]), .pin13(n74151_15_pin13[5]), .pin12(n74151_15_pin12[5]), .pin11(S0),
    .pin10(n74151_1_pin10), .pin9(n74151_1_pin9));  // open: pin6
  _74151 #(.VccGndPorts("true")) u_74151_9 (
    .pin1(n74151_15_pin1[6]), .pin2(n74151_15_pin2[6]), .pin3(INPUT1[6]), .pin4(INPUT0[6]),
    .pin5(DATAOUT[6]), .pin7(n74151_1_pin7), .pin8(GND), .pin16(VCC), .pin15(n74151_15_pin15[6]),
    .pin14(n74151_15_pin14[6]), .pin13(n74151_15_pin13[6]), .pin12(n74151_15_pin12[6]), .pin11(S0),
    .pin10(n74151_1_pin10), .pin9(n74151_1_pin9));  // open: pin6
  _74151 #(.VccGndPorts("true")) u_74151_10 (
    .pin1(n74151_15_pin1[7]), .pin2(n74151_15_pin2[7]), .pin3(INPUT1[7]), .pin4(INPUT0[7]),
    .pin5(DATAOUT[7]), .pin7(n74151_1_pin7), .pin8(GND), .pin16(VCC), .pin15(n74151_15_pin15[7]),
    .pin14(n74151_15_pin14[7]), .pin13(n74151_15_pin13[7]), .pin12(n74151_15_pin12[7]), .pin11(S0),
    .pin10(n74151_1_pin10), .pin9(n74151_1_pin9));  // open: pin6
  _74151 #(.VccGndPorts("true")) u_74151_11 (
    .pin1(n74151_15_pin1[8]), .pin2(n74151_15_pin2[8]), .pin3(INPUT1[8]), .pin4(INPUT0[8]),
    .pin5(DATAOUT[8]), .pin7(n74151_1_pin7), .pin8(GND), .pin16(VCC), .pin15(n74151_15_pin15[8]),
    .pin14(n74151_15_pin14[8]), .pin13(n74151_15_pin13[8]), .pin12(n74151_15_pin12[8]), .pin11(S0),
    .pin10(n74151_1_pin10), .pin9(n74151_1_pin9));  // open: pin6
  _74151 #(.VccGndPorts("true")) u_74151_12 (
    .pin1(n74151_15_pin1[9]), .pin2(n74151_15_pin2[9]), .pin3(INPUT1[9]), .pin4(INPUT0[9]),
    .pin5(DATAOUT[9]), .pin7(n74151_1_pin7), .pin8(GND), .pin16(VCC), .pin15(n74151_15_pin15[9]),
    .pin14(n74151_15_pin14[9]), .pin13(n74151_15_pin13[9]), .pin12(n74151_15_pin12[9]), .pin11(S0),
    .pin10(n74151_1_pin10), .pin9(n74151_1_pin9));  // open: pin6
  _74151 #(.VccGndPorts("true")) u_74151_13 (
    .pin1(n74151_15_pin1[10]), .pin2(n74151_15_pin2[10]), .pin3(INPUT1[10]), .pin4(INPUT0[10]),
    .pin5(DATAOUT[10]), .pin7(n74151_1_pin7), .pin8(GND), .pin16(VCC), .pin15(n74151_15_pin15[10]),
    .pin14(n74151_15_pin14[10]), .pin13(n74151_15_pin13[10]), .pin12(n74151_15_pin12[10]), .pin11(S0),
    .pin10(n74151_1_pin10), .pin9(n74151_1_pin9));  // open: pin6
  _74151 #(.VccGndPorts("true")) u_74151_14 (
    .pin1(n74151_15_pin1[11]), .pin2(n74151_15_pin2[11]), .pin3(INPUT1[11]), .pin4(INPUT0[11]),
    .pin5(DATAOUT[11]), .pin7(n74151_1_pin7), .pin8(GND), .pin16(VCC), .pin15(n74151_15_pin15[11]),
    .pin14(n74151_15_pin14[11]), .pin13(n74151_15_pin13[11]), .pin12(n74151_15_pin12[11]), .pin11(S0),
    .pin10(n74151_1_pin10), .pin9(n74151_1_pin9));  // open: pin6
  _74151 #(.VccGndPorts("true")) u_74151_15 (
    .pin1(n74151_15_pin1[0]), .pin2(n74151_15_pin2[0]), .pin3(INPUT1[0]), .pin4(INPUT0[0]),
    .pin5(DATAOUT[0]), .pin7(n74151_1_pin7), .pin8(GND), .pin16(VCC), .pin15(n74151_15_pin15[0]),
    .pin14(n74151_15_pin14[0]), .pin13(n74151_15_pin13[0]), .pin12(n74151_15_pin12[0]), .pin11(S0),
    .pin10(n74151_1_pin10), .pin9(n74151_1_pin9));  // open: pin6
  _74151 #(.VccGndPorts("true")) u_74151_16 (
    .pin1(n74151_15_pin1[1]), .pin2(n74151_15_pin2[1]), .pin3(INPUT1[1]), .pin4(INPUT0[1]),
    .pin5(DATAOUT[1]), .pin7(n74151_1_pin7), .pin8(GND), .pin16(VCC), .pin15(n74151_15_pin15[1]),
    .pin14(n74151_15_pin14[1]), .pin13(n74151_15_pin13[1]), .pin12(n74151_15_pin12[1]), .pin11(S0),
    .pin10(n74151_1_pin10), .pin9(n74151_1_pin9));  // open: pin6
  not not_1 (n74151_1_pin7, ENActiveHigh);
  // also tied to GND on the sheet: {n74151_1_pin10, n74151_1_pin9}

  // Notes on the sheet:
  //   INPUT0
  //   VCC
  //   INPUT7
  //   INPUT6
  //   INPUT5
  //   INPUT4
  //   INPUT3
  //   INPUT2
  //   INPUT1
  //   GND
  //   OUT
endmodule

module arithmaticCirc (
  input  GND,
  input  VCC,
  input  [15:0] AIN,
  input  [15:0] BIN,
  input  S1,
  input  S0,
  input  CIN,
  output [15:0] OUTARITH,
  output COUT
);

  wire n74151_1_pin1, n74151_1_pin2, n74151_1_pin3, n74151_1_pin5, n74151_1_pin9, n74151_2_pin1,
       n74151_2_pin2, n74151_2_pin3, n74151_2_pin5, n74151_3_pin1, n74151_3_pin2, n74151_3_pin3,
       n74151_3_pin5, n74151_4_pin1, n74151_4_pin2, n74151_4_pin3, n74151_4_pin5, n74151_5_pin1,
       n74151_5_pin2, n74151_5_pin3, n74151_5_pin5, n74151_6_pin1, n74151_6_pin2, n74151_6_pin3,
       n74151_6_pin5, n74151_7_pin1, n74151_7_pin2, n74151_7_pin3, n74151_7_pin5, n74151_8_pin1,
       n74151_8_pin2, n74151_8_pin3, n74151_8_pin5, n74151_9_pin1, n74151_9_pin2, n74151_9_pin3,
       n74151_9_pin5, n74151_10_pin1, n74151_10_pin2, n74151_10_pin3, n74151_10_pin5, n74151_11_pin1,
       n74151_11_pin2, n74151_11_pin3, n74151_11_pin5, n74151_12_pin1, n74151_12_pin2, n74151_12_pin3,
       n74151_12_pin5, n74151_13_pin1, n74151_13_pin2, n74151_13_pin3, n74151_13_pin5, n74151_14_pin1,
       n74151_14_pin2, n74151_14_pin3, n74151_14_pin5, n74151_15_pin1, n74151_15_pin2, n74151_15_pin3,
       n74151_15_pin5, n74151_16_pin1, n74151_16_pin2, n74151_16_pin3, n74151_16_pin5, n74283_1_pin9,
       n74283_2_pin7, n74283_3_pin9;

  _74151 #(.VccGndPorts("true")) u_74151_1 (
    .pin1(n74151_1_pin1), .pin2(n74151_1_pin2), .pin3(n74151_1_pin3), .pin4(BIN[0]), .pin5(n74151_1_pin5),
    .pin8(GND), .pin16(VCC), .pin11(S0), .pin10(S1), .pin9(n74151_1_pin9));  // open: pin6, pin7, pin15, pin14, pin13, pin12
  _74151 #(.VccGndPorts("true")) u_74151_2 (
    .pin1(n74151_2_pin1), .pin2(n74151_2_pin2), .pin3(n74151_2_pin3), .pin4(BIN[10]), .pin5(n74151_2_pin5),
    .pin8(GND), .pin16(VCC), .pin11(S0), .pin10(S1), .pin9(n74151_1_pin9));  // open: pin6, pin7, pin15, pin14, pin13, pin12
  _74151 #(.VccGndPorts("true")) u_74151_3 (
    .pin1(n74151_3_pin1), .pin2(n74151_3_pin2), .pin3(n74151_3_pin3), .pin4(BIN[13]), .pin5(n74151_3_pin5),
    .pin8(GND), .pin16(VCC), .pin11(S0), .pin10(S1), .pin9(n74151_1_pin9));  // open: pin6, pin7, pin15, pin14, pin13, pin12
  _74151 #(.VccGndPorts("true")) u_74151_4 (
    .pin1(n74151_4_pin1), .pin2(n74151_4_pin2), .pin3(n74151_4_pin3), .pin4(BIN[15]), .pin5(n74151_4_pin5),
    .pin8(GND), .pin16(VCC), .pin11(S0), .pin10(S1), .pin9(n74151_1_pin9));  // open: pin6, pin7, pin15, pin14, pin13, pin12
  not not_1 (n74151_1_pin3, BIN[0]);
  _74151 #(.VccGndPorts("true")) u_74151_5 (
    .pin1(n74151_5_pin1), .pin2(n74151_5_pin2), .pin3(n74151_5_pin3), .pin4(BIN[1]), .pin5(n74151_5_pin5),
    .pin8(GND), .pin16(VCC), .pin11(S0), .pin10(S1), .pin9(n74151_1_pin9));  // open: pin6, pin7, pin15, pin14, pin13, pin12
  not not_2 (n74151_5_pin3, BIN[1]);
  _74151 #(.VccGndPorts("true")) u_74151_6 (
    .pin1(n74151_6_pin1), .pin2(n74151_6_pin2), .pin3(n74151_6_pin3), .pin4(BIN[2]), .pin5(n74151_6_pin5),
    .pin8(GND), .pin16(VCC), .pin11(S0), .pin10(S1), .pin9(n74151_1_pin9));  // open: pin6, pin7, pin15, pin14, pin13, pin12
  not not_3 (n74151_6_pin3, BIN[2]);
  _74151 #(.VccGndPorts("true")) u_74151_7 (
    .pin1(n74151_7_pin1), .pin2(n74151_7_pin2), .pin3(n74151_7_pin3), .pin4(BIN[3]), .pin5(n74151_7_pin5),
    .pin8(GND), .pin16(VCC), .pin11(S0), .pin10(S1), .pin9(n74151_1_pin9));  // open: pin6, pin7, pin15, pin14, pin13, pin12
  not not_4 (n74151_7_pin3, BIN[3]);
  _74151 #(.VccGndPorts("true")) u_74151_8 (
    .pin1(n74151_8_pin1), .pin2(n74151_8_pin2), .pin3(n74151_8_pin3), .pin4(BIN[4]), .pin5(n74151_8_pin5),
    .pin8(GND), .pin16(VCC), .pin11(S0), .pin10(S1), .pin9(n74151_1_pin9));  // open: pin6, pin7, pin15, pin14, pin13, pin12
  not not_5 (n74151_8_pin3, BIN[4]);
  _74151 #(.VccGndPorts("true")) u_74151_9 (
    .pin1(n74151_9_pin1), .pin2(n74151_9_pin2), .pin3(n74151_9_pin3), .pin4(BIN[5]), .pin5(n74151_9_pin5),
    .pin8(GND), .pin16(VCC), .pin11(S0), .pin10(S1), .pin9(n74151_1_pin9));  // open: pin6, pin7, pin15, pin14, pin13, pin12
  not not_6 (n74151_9_pin3, BIN[5]);
  _74151 #(.VccGndPorts("true")) u_74151_10 (
    .pin1(n74151_10_pin1), .pin2(n74151_10_pin2), .pin3(n74151_10_pin3), .pin4(BIN[6]),
    .pin5(n74151_10_pin5), .pin8(GND), .pin16(VCC), .pin11(S0), .pin10(S1), .pin9(n74151_1_pin9));  // open: pin6, pin7, pin15, pin14, pin13, pin12
  not not_7 (n74151_10_pin3, BIN[6]);
  _74151 #(.VccGndPorts("true")) u_74151_11 (
    .pin1(n74151_11_pin1), .pin2(n74151_11_pin2), .pin3(n74151_11_pin3), .pin4(BIN[7]),
    .pin5(n74151_11_pin5), .pin8(GND), .pin16(VCC), .pin11(S0), .pin10(S1), .pin9(n74151_1_pin9));  // open: pin6, pin7, pin15, pin14, pin13, pin12
  not not_8 (n74151_11_pin3, BIN[7]);
  _74151 #(.VccGndPorts("true")) u_74151_12 (
    .pin1(n74151_12_pin1), .pin2(n74151_12_pin2), .pin3(n74151_12_pin3), .pin4(BIN[8]),
    .pin5(n74151_12_pin5), .pin8(GND), .pin16(VCC), .pin11(S0), .pin10(S1), .pin9(n74151_1_pin9));  // open: pin6, pin7, pin15, pin14, pin13, pin12
  not not_9 (n74151_12_pin3, BIN[8]);
  _74151 #(.VccGndPorts("true")) u_74151_13 (
    .pin1(n74151_13_pin1), .pin2(n74151_13_pin2), .pin3(n74151_13_pin3), .pin4(BIN[9]),
    .pin5(n74151_13_pin5), .pin8(GND), .pin16(VCC), .pin11(S0), .pin10(S1), .pin9(n74151_1_pin9));  // open: pin6, pin7, pin15, pin14, pin13, pin12
  not not_10 (n74151_2_pin3, BIN[10]);
  _74151 #(.VccGndPorts("true")) u_74151_14 (
    .pin1(n74151_14_pin1), .pin2(n74151_14_pin2), .pin3(n74151_14_pin3), .pin4(BIN[11]),
    .pin5(n74151_14_pin5), .pin8(GND), .pin16(VCC), .pin11(S0), .pin10(S1), .pin9(n74151_1_pin9));  // open: pin6, pin7, pin15, pin14, pin13, pin12
  not not_11 (n74151_14_pin3, BIN[11]);
  _74151 #(.VccGndPorts("true")) u_74151_15 (
    .pin1(n74151_15_pin1), .pin2(n74151_15_pin2), .pin3(n74151_15_pin3), .pin4(BIN[12]),
    .pin5(n74151_15_pin5), .pin8(GND), .pin16(VCC), .pin11(S0), .pin10(S1), .pin9(n74151_1_pin9));  // open: pin6, pin7, pin15, pin14, pin13, pin12
  not not_12 (n74151_3_pin3, BIN[13]);
  _74151 #(.VccGndPorts("true")) u_74151_16 (
    .pin1(n74151_16_pin1), .pin2(n74151_16_pin2), .pin3(n74151_16_pin3), .pin4(BIN[14]),
    .pin5(n74151_16_pin5), .pin8(GND), .pin16(VCC), .pin11(S0), .pin10(S1), .pin9(n74151_1_pin9));  // open: pin6, pin7, pin15, pin14, pin13, pin12
  not not_13 (n74151_16_pin3, BIN[14]);
  not not_14 (n74151_4_pin3, BIN[15]);
  not not_15 (n74151_13_pin3, BIN[9]);
  not not_16 (n74151_15_pin3, BIN[12]);
  _74283 #(.VccGndPorts("true")) u_74283_1 (
    .pin1(OUTARITH[1]), .pin2(n74151_5_pin5), .pin3(AIN[1]), .pin4(OUTARITH[0]), .pin5(AIN[0]),
    .pin6(n74151_1_pin5), .pin7(CIN), .pin8(GND), .pin16(VCC), .pin15(n74151_6_pin5), .pin14(AIN[2]),
    .pin13(OUTARITH[2]), .pin12(AIN[3]), .pin11(n74151_7_pin5), .pin10(OUTARITH[3]), .pin9(n74283_1_pin9));
  _74283 #(.VccGndPorts("true")) u_74283_2 (
    .pin1(OUTARITH[13]), .pin2(n74151_3_pin5), .pin3(AIN[13]), .pin4(OUTARITH[12]), .pin5(AIN[12]),
    .pin6(n74151_15_pin5), .pin7(n74283_2_pin7), .pin8(GND), .pin16(VCC), .pin15(n74151_16_pin5),
    .pin14(AIN[14]), .pin13(OUTARITH[14]), .pin12(AIN[15]), .pin11(n74151_4_pin5), .pin10(OUTARITH[15]),
    .pin9(COUT));
  _74283 #(.VccGndPorts("true")) u_74283_3 (
    .pin1(OUTARITH[5]), .pin2(n74151_9_pin5), .pin3(AIN[5]), .pin4(OUTARITH[4]), .pin5(AIN[4]),
    .pin6(n74151_8_pin5), .pin7(n74283_1_pin9), .pin8(GND), .pin16(VCC), .pin15(n74151_10_pin5),
    .pin14(AIN[6]), .pin13(OUTARITH[6]), .pin12(AIN[7]), .pin11(n74151_11_pin5), .pin10(OUTARITH[7]),
    .pin9(n74283_3_pin9));
  _74283 #(.VccGndPorts("true")) u_74283_4 (
    .pin1(OUTARITH[9]), .pin2(n74151_13_pin5), .pin3(AIN[9]), .pin4(OUTARITH[8]), .pin5(AIN[8]),
    .pin6(n74151_12_pin5), .pin7(n74283_3_pin9), .pin8(GND), .pin16(VCC), .pin15(n74151_2_pin5),
    .pin14(AIN[10]), .pin13(OUTARITH[10]), .pin12(AIN[11]), .pin11(n74151_14_pin5), .pin10(OUTARITH[11]),
    .pin9(n74283_2_pin7));
  // also tied to GND on the sheet: {n74151_4_pin2, n74151_1_pin2, n74151_2_pin2, n74151_3_pin2, n74151_5_pin2, n74151_9_pin2, n74151_10_pin2, n74151_6_pin2, n74151_8_pin2, n74151_11_pin2, n74151_7_pin2, n74151_12_pin2, n74151_14_pin2, n74151_16_pin2, n74151_13_pin2, n74151_15_pin2}
  // also tied to VCC on the sheet: {n74151_4_pin1, n74151_1_pin1, n74151_2_pin1, n74151_3_pin1, n74151_5_pin1, n74151_9_pin1, n74151_10_pin1, n74151_6_pin1, n74151_8_pin1, n74151_11_pin1, n74151_7_pin1, n74151_12_pin1, n74151_14_pin1, n74151_16_pin1, n74151_13_pin1, n74151_15_pin1}

  // Notes on the sheet:
  //   0-> A+B
  //   1-> A + ~B
  //   2-> A + 0
  //   3-> A + -1
  //   B15
  //   B11
  //   B12
  //   B7
  //   B8
  //   B3
  //   B4
  //   B0
endmodule

module logicCirc (
  input  VCC,
  input  [15:0] BIN,
  input  ENActiveHigh,
  input  [15:0] AIN,
  input  S0,
  input  S1,
  input  GND,
  output [15:0] OUTLOGIC
);

  wire [15:0] n7404_1_pin12, n7408_1_pin3, n7432_1_pin3, n7486_1_pin3;

  _7408 #(.VccGndPorts("true")) u_7408_1 (
    .pin1(AIN[0]), .pin2(BIN[0]), .pin3(n7408_1_pin3[0]), .pin4(AIN[1]), .pin5(BIN[1]),
    .pin6(n7408_1_pin3[1]), .pin7(GND), .pin14(VCC), .pin13(AIN[2]), .pin12(BIN[2]), .pin11(n7408_1_pin3[2]),
    .pin10(AIN[3]), .pin9(BIN[3]), .pin8(n7408_1_pin3[3]));
  _7408 #(.VccGndPorts("true")) u_7408_2 (
    .pin1(AIN[4]), .pin2(BIN[4]), .pin3(n7408_1_pin3[4]), .pin4(AIN[5]), .pin5(BIN[5]),
    .pin6(n7408_1_pin3[5]), .pin7(GND), .pin14(VCC), .pin13(AIN[6]), .pin12(BIN[6]), .pin11(n7408_1_pin3[6]),
    .pin10(AIN[7]), .pin9(BIN[7]), .pin8(n7408_1_pin3[7]));
  _7408 #(.VccGndPorts("true")) u_7408_3 (
    .pin1(AIN[8]), .pin2(BIN[8]), .pin3(n7408_1_pin3[8]), .pin4(AIN[9]), .pin5(BIN[9]),
    .pin6(n7408_1_pin3[9]), .pin7(GND), .pin14(VCC), .pin13(AIN[10]), .pin12(BIN[10]),
    .pin11(n7408_1_pin3[10]), .pin10(AIN[11]), .pin9(BIN[11]), .pin8(n7408_1_pin3[11]));
  _7408 #(.VccGndPorts("true")) u_7408_4 (
    .pin1(AIN[12]), .pin2(BIN[12]), .pin3(n7408_1_pin3[12]), .pin4(AIN[13]), .pin5(BIN[13]),
    .pin6(n7408_1_pin3[13]), .pin7(GND), .pin14(VCC), .pin13(AIN[14]), .pin12(BIN[14]),
    .pin11(n7408_1_pin3[14]), .pin10(AIN[15]), .pin9(BIN[15]), .pin8(n7408_1_pin3[15]));
  _7432 #(.VccGndPorts("true")) u_7432_1 (
    .pin1(AIN[0]), .pin2(BIN[0]), .pin3(n7432_1_pin3[0]), .pin4(AIN[1]), .pin5(BIN[1]),
    .pin6(n7432_1_pin3[1]), .pin7(GND), .pin14(VCC), .pin13(AIN[2]), .pin12(BIN[2]), .pin11(n7432_1_pin3[2]),
    .pin10(AIN[3]), .pin9(BIN[3]), .pin8(n7432_1_pin3[3]));
  _7432 #(.VccGndPorts("true")) u_7432_2 (
    .pin1(AIN[4]), .pin2(BIN[4]), .pin3(n7432_1_pin3[4]), .pin4(AIN[5]), .pin5(BIN[5]),
    .pin6(n7432_1_pin3[5]), .pin7(GND), .pin14(VCC), .pin13(AIN[6]), .pin12(BIN[6]), .pin11(n7432_1_pin3[6]),
    .pin10(AIN[7]), .pin9(BIN[7]), .pin8(n7432_1_pin3[7]));
  _7432 #(.VccGndPorts("true")) u_7432_3 (
    .pin1(AIN[8]), .pin2(BIN[8]), .pin3(n7432_1_pin3[8]), .pin4(AIN[9]), .pin5(BIN[9]),
    .pin6(n7432_1_pin3[9]), .pin7(GND), .pin14(VCC), .pin13(AIN[10]), .pin12(BIN[10]),
    .pin11(n7432_1_pin3[10]), .pin10(AIN[11]), .pin9(BIN[11]), .pin8(n7432_1_pin3[11]));
  _7432 #(.VccGndPorts("true")) u_7432_4 (
    .pin1(AIN[12]), .pin2(BIN[12]), .pin3(n7432_1_pin3[12]), .pin4(AIN[13]), .pin5(BIN[13]),
    .pin6(n7432_1_pin3[13]), .pin7(GND), .pin14(VCC), .pin13(AIN[14]), .pin12(BIN[14]),
    .pin11(n7432_1_pin3[14]), .pin10(AIN[15]), .pin9(BIN[15]), .pin8(n7432_1_pin3[15]));
  _7486 #(.VccGndPorts("true")) u_7486_1 (
    .pin1(AIN[0]), .pin2(BIN[0]), .pin3(n7486_1_pin3[0]), .pin4(AIN[1]), .pin5(BIN[1]),
    .pin6(n7486_1_pin3[1]), .pin7(GND), .pin14(VCC), .pin13(AIN[2]), .pin12(BIN[2]), .pin11(n7486_1_pin3[2]),
    .pin10(AIN[3]), .pin9(BIN[3]), .pin8(n7486_1_pin3[3]));
  _7486 #(.VccGndPorts("true")) u_7486_2 (
    .pin1(AIN[4]), .pin2(BIN[4]), .pin3(n7486_1_pin3[4]), .pin4(AIN[5]), .pin5(BIN[5]),
    .pin6(n7486_1_pin3[5]), .pin7(GND), .pin14(VCC), .pin13(AIN[6]), .pin12(BIN[6]), .pin11(n7486_1_pin3[6]),
    .pin10(AIN[7]), .pin9(BIN[7]), .pin8(n7486_1_pin3[7]));
  _7486 #(.VccGndPorts("true")) u_7486_3 (
    .pin1(AIN[8]), .pin2(BIN[8]), .pin3(n7486_1_pin3[8]), .pin4(AIN[9]), .pin5(BIN[9]),
    .pin6(n7486_1_pin3[9]), .pin7(GND), .pin14(VCC), .pin13(AIN[10]), .pin12(BIN[10]),
    .pin11(n7486_1_pin3[10]), .pin10(AIN[11]), .pin9(BIN[11]), .pin8(n7486_1_pin3[11]));
  _7486 #(.VccGndPorts("true")) u_7486_4 (
    .pin1(AIN[12]), .pin2(BIN[12]), .pin3(n7486_1_pin3[12]), .pin4(AIN[13]), .pin5(BIN[13]),
    .pin6(n7486_1_pin3[13]), .pin7(GND), .pin14(VCC), .pin13(AIN[14]), .pin12(BIN[14]),
    .pin11(n7486_1_pin3[14]), .pin10(AIN[15]), .pin9(BIN[15]), .pin8(n7486_1_pin3[15]));
  _7404 #(.VccGndPorts("true")) u_7404_1 (
    .pin1(AIN[2]), .pin2(n7404_1_pin12[2]), .pin3(AIN[3]), .pin4(n7404_1_pin12[3]), .pin7(GND), .pin14(VCC),
    .pin13(AIN[0]), .pin12(n7404_1_pin12[0]), .pin11(AIN[1]), .pin10(n7404_1_pin12[1]));  // open: pin5, pin6, pin9, pin8
  _7404 #(.VccGndPorts("true")) u_7404_2 (
    .pin1(AIN[6]), .pin2(n7404_1_pin12[6]), .pin3(AIN[7]), .pin4(n7404_1_pin12[7]), .pin7(GND), .pin14(VCC),
    .pin13(AIN[4]), .pin12(n7404_1_pin12[4]), .pin11(AIN[5]), .pin10(n7404_1_pin12[5]));  // open: pin5, pin6, pin9, pin8
  _7404 #(.VccGndPorts("true")) u_7404_3 (
    .pin1(AIN[10]), .pin2(n7404_1_pin12[10]), .pin3(AIN[11]), .pin4(n7404_1_pin12[11]), .pin7(GND),
    .pin14(VCC), .pin13(AIN[8]), .pin12(n7404_1_pin12[8]), .pin11(AIN[9]), .pin10(n7404_1_pin12[9]));  // open: pin5, pin6, pin9, pin8
  _7404 #(.VccGndPorts("true")) u_7404_4 (
    .pin1(AIN[14]), .pin2(n7404_1_pin12[14]), .pin3(AIN[15]), .pin4(n7404_1_pin12[15]), .pin7(GND),
    .pin14(VCC), .pin13(AIN[12]), .pin12(n7404_1_pin12[12]), .pin11(AIN[13]), .pin10(n7404_1_pin12[13]));  // open: pin5, pin6, pin9, pin8
  sixteenFourToOneMultiplexer sixteenfourtoonemultiplexer_1 (
    .ENActiveHigh(ENActiveHigh), .GND(GND), .VCC(VCC), .S0(S0), .S1(S1), .INPUT0(n7408_1_pin3),
    .INPUT1(n7432_1_pin3), .INPUT2(n7486_1_pin3), .INPUT3(n7404_1_pin12), .DATAOUT(OUTLOGIC));

  // Notes on the sheet:
  //   B0
  //   B4
  //   B8
  //   B12
  //   B15
  //   B0
  //   B4
  //   B8
  //   B12
  //   B15
  //   B0
  //   B4
  //   B8
  //   B12
  //   B15
  //   B0
  //   B4
  //   B8
  //   B12
  //   AND
  //   OR
  //   XOR
endmodule

module sixteenFourToOneMultiplexer (
  input  ENActiveHigh,
  input  GND,
  input  VCC,
  input  S0,
  input  S1,
  input  [15:0] INPUT0,
  input  [15:0] INPUT1,
  input  [15:0] INPUT2,
  input  [15:0] INPUT3,
  output [15:0] DATAOUT
);

  wire n74151_1_pin7, n74151_1_pin9;
  wire [15:0] n74151_15_pin12, n74151_15_pin13, n74151_15_pin14, n74151_15_pin15;

  _74151 #(.VccGndPorts("true")) u_74151_1 (
    .pin1(INPUT3[12]), .pin2(INPUT2[12]), .pin3(INPUT1[12]), .pin4(INPUT0[12]), .pin5(DATAOUT[12]),
    .pin7(n74151_1_pin7), .pin8(GND), .pin16(VCC), .pin15(n74151_15_pin15[12]), .pin14(n74151_15_pin14[12]),
    .pin13(n74151_15_pin13[12]), .pin12(n74151_15_pin12[12]), .pin11(S0), .pin10(S1), .pin9(n74151_1_pin9));  // open: pin6
  _74151 #(.VccGndPorts("true")) u_74151_2 (
    .pin1(INPUT3[13]), .pin2(INPUT2[13]), .pin3(INPUT1[13]), .pin4(INPUT0[13]), .pin5(DATAOUT[13]),
    .pin7(n74151_1_pin7), .pin8(GND), .pin16(VCC), .pin15(n74151_15_pin15[13]), .pin14(n74151_15_pin14[13]),
    .pin13(n74151_15_pin13[13]), .pin12(n74151_15_pin12[13]), .pin11(S0), .pin10(S1), .pin9(n74151_1_pin9));  // open: pin6
  _74151 #(.VccGndPorts("true")) u_74151_3 (
    .pin1(INPUT3[14]), .pin2(INPUT2[14]), .pin3(INPUT1[14]), .pin4(INPUT0[14]), .pin5(DATAOUT[14]),
    .pin7(n74151_1_pin7), .pin8(GND), .pin16(VCC), .pin15(n74151_15_pin15[14]), .pin14(n74151_15_pin14[14]),
    .pin13(n74151_15_pin13[14]), .pin12(n74151_15_pin12[14]), .pin11(S0), .pin10(S1), .pin9(n74151_1_pin9));  // open: pin6
  _74151 #(.VccGndPorts("true")) u_74151_4 (
    .pin1(INPUT3[15]), .pin2(INPUT2[15]), .pin3(INPUT1[15]), .pin4(INPUT0[15]), .pin5(DATAOUT[15]),
    .pin7(n74151_1_pin7), .pin8(GND), .pin16(VCC), .pin15(n74151_15_pin15[15]), .pin14(n74151_15_pin14[15]),
    .pin13(n74151_15_pin13[15]), .pin12(n74151_15_pin12[15]), .pin11(S0), .pin10(S1), .pin9(n74151_1_pin9));  // open: pin6
  _74151 #(.VccGndPorts("true")) u_74151_5 (
    .pin1(INPUT3[2]), .pin2(INPUT2[2]), .pin3(INPUT1[2]), .pin4(INPUT0[2]), .pin5(DATAOUT[2]),
    .pin7(n74151_1_pin7), .pin8(GND), .pin16(VCC), .pin15(n74151_15_pin15[2]), .pin14(n74151_15_pin14[2]),
    .pin13(n74151_15_pin13[2]), .pin12(n74151_15_pin12[2]), .pin11(S0), .pin10(S1), .pin9(n74151_1_pin9));  // open: pin6
  _74151 #(.VccGndPorts("true")) u_74151_6 (
    .pin1(INPUT3[3]), .pin2(INPUT2[3]), .pin3(INPUT1[3]), .pin4(INPUT0[3]), .pin5(DATAOUT[3]),
    .pin7(n74151_1_pin7), .pin8(GND), .pin16(VCC), .pin15(n74151_15_pin15[3]), .pin14(n74151_15_pin14[3]),
    .pin13(n74151_15_pin13[3]), .pin12(n74151_15_pin12[3]), .pin11(S0), .pin10(S1), .pin9(n74151_1_pin9));  // open: pin6
  _74151 #(.VccGndPorts("true")) u_74151_7 (
    .pin1(INPUT3[4]), .pin2(INPUT2[4]), .pin3(INPUT1[4]), .pin4(INPUT0[4]), .pin5(DATAOUT[4]),
    .pin7(n74151_1_pin7), .pin8(GND), .pin16(VCC), .pin15(n74151_15_pin15[4]), .pin14(n74151_15_pin14[4]),
    .pin13(n74151_15_pin13[4]), .pin12(n74151_15_pin12[4]), .pin11(S0), .pin10(S1), .pin9(n74151_1_pin9));  // open: pin6
  _74151 #(.VccGndPorts("true")) u_74151_8 (
    .pin1(INPUT3[5]), .pin2(INPUT2[5]), .pin3(INPUT1[5]), .pin4(INPUT0[5]), .pin5(DATAOUT[5]),
    .pin7(n74151_1_pin7), .pin8(GND), .pin16(VCC), .pin15(n74151_15_pin15[5]), .pin14(n74151_15_pin14[5]),
    .pin13(n74151_15_pin13[5]), .pin12(n74151_15_pin12[5]), .pin11(S0), .pin10(S1), .pin9(n74151_1_pin9));  // open: pin6
  _74151 #(.VccGndPorts("true")) u_74151_9 (
    .pin1(INPUT3[6]), .pin2(INPUT2[6]), .pin3(INPUT1[6]), .pin4(INPUT0[6]), .pin5(DATAOUT[6]),
    .pin7(n74151_1_pin7), .pin8(GND), .pin16(VCC), .pin15(n74151_15_pin15[6]), .pin14(n74151_15_pin14[6]),
    .pin13(n74151_15_pin13[6]), .pin12(n74151_15_pin12[6]), .pin11(S0), .pin10(S1), .pin9(n74151_1_pin9));  // open: pin6
  _74151 #(.VccGndPorts("true")) u_74151_10 (
    .pin1(INPUT3[7]), .pin2(INPUT2[7]), .pin3(INPUT1[7]), .pin4(INPUT0[7]), .pin5(DATAOUT[7]),
    .pin7(n74151_1_pin7), .pin8(GND), .pin16(VCC), .pin15(n74151_15_pin15[7]), .pin14(n74151_15_pin14[7]),
    .pin13(n74151_15_pin13[7]), .pin12(n74151_15_pin12[7]), .pin11(S0), .pin10(S1), .pin9(n74151_1_pin9));  // open: pin6
  _74151 #(.VccGndPorts("true")) u_74151_11 (
    .pin1(INPUT3[8]), .pin2(INPUT2[8]), .pin3(INPUT1[8]), .pin4(INPUT0[8]), .pin5(DATAOUT[8]),
    .pin7(n74151_1_pin7), .pin8(GND), .pin16(VCC), .pin15(n74151_15_pin15[8]), .pin14(n74151_15_pin14[8]),
    .pin13(n74151_15_pin13[8]), .pin12(n74151_15_pin12[8]), .pin11(S0), .pin10(S1), .pin9(n74151_1_pin9));  // open: pin6
  _74151 #(.VccGndPorts("true")) u_74151_12 (
    .pin1(INPUT3[9]), .pin2(INPUT2[9]), .pin3(INPUT1[9]), .pin4(INPUT0[9]), .pin5(DATAOUT[9]),
    .pin7(n74151_1_pin7), .pin8(GND), .pin16(VCC), .pin15(n74151_15_pin15[9]), .pin14(n74151_15_pin14[9]),
    .pin13(n74151_15_pin13[9]), .pin12(n74151_15_pin12[9]), .pin11(S0), .pin10(S1), .pin9(n74151_1_pin9));  // open: pin6
  _74151 #(.VccGndPorts("true")) u_74151_13 (
    .pin1(INPUT3[10]), .pin2(INPUT2[10]), .pin3(INPUT1[10]), .pin4(INPUT0[10]), .pin5(DATAOUT[10]),
    .pin7(n74151_1_pin7), .pin8(GND), .pin16(VCC), .pin15(n74151_15_pin15[10]), .pin14(n74151_15_pin14[10]),
    .pin13(n74151_15_pin13[10]), .pin12(n74151_15_pin12[10]), .pin11(S0), .pin10(S1), .pin9(n74151_1_pin9));  // open: pin6
  _74151 #(.VccGndPorts("true")) u_74151_14 (
    .pin1(INPUT3[11]), .pin2(INPUT2[11]), .pin3(INPUT1[11]), .pin4(INPUT0[11]), .pin5(DATAOUT[11]),
    .pin7(n74151_1_pin7), .pin8(GND), .pin16(VCC), .pin15(n74151_15_pin15[11]), .pin14(n74151_15_pin14[11]),
    .pin13(n74151_15_pin13[11]), .pin12(n74151_15_pin12[11]), .pin11(S0), .pin10(S1), .pin9(n74151_1_pin9));  // open: pin6
  _74151 #(.VccGndPorts("true")) u_74151_15 (
    .pin1(INPUT3[0]), .pin2(INPUT2[0]), .pin3(INPUT1[0]), .pin4(INPUT0[0]), .pin5(DATAOUT[0]),
    .pin7(n74151_1_pin7), .pin8(GND), .pin16(VCC), .pin15(n74151_15_pin15[0]), .pin14(n74151_15_pin14[0]),
    .pin13(n74151_15_pin13[0]), .pin12(n74151_15_pin12[0]), .pin11(S0), .pin10(S1), .pin9(n74151_1_pin9));  // open: pin6
  _74151 #(.VccGndPorts("true")) u_74151_16 (
    .pin1(INPUT3[1]), .pin2(INPUT2[1]), .pin3(INPUT1[1]), .pin4(INPUT0[1]), .pin5(DATAOUT[1]),
    .pin7(n74151_1_pin7), .pin8(GND), .pin16(VCC), .pin15(n74151_15_pin15[1]), .pin14(n74151_15_pin14[1]),
    .pin13(n74151_15_pin13[1]), .pin12(n74151_15_pin12[1]), .pin11(S0), .pin10(S1), .pin9(n74151_1_pin9));  // open: pin6
  not not_1 (n74151_1_pin7, ENActiveHigh);

  // Notes on the sheet:
  //   INPUT0
  //   VCC
  //   INPUT7
  //   INPUT6
  //   INPUT5
  //   INPUT4
  //   INPUT3
  //   INPUT2
  //   INPUT1
  //   GND
  //   OUT
endmodule

module twoElevenToOneDemultiplexer (
);

  _74139 u_74139_1 ();  // open: pin1, pin2, pin3, pin4, pin5, pin6, pin7, pin15, pin14, pin13, pin12, pin11, pin10, pin9
endmodule

module shiftCirc (
  input  VCC,
  input  GND,
  input  S0,
  input  LSBIN,
  input  MSBIN,
  input  [15:0] AIN,
  output [15:0] SHIFTOUT
);

  wire n74151_1_pin10;

  _74151 #(.VccGndPorts("true")) u_74151_1 (
    .pin3(AIN[1]), .pin4(LSBIN), .pin5(SHIFTOUT[0]), .pin8(GND), .pin16(VCC), .pin11(S0),
    .pin10(n74151_1_pin10), .pin9(n74151_1_pin10));  // open: pin1, pin2, pin6, pin7, pin15, pin14, pin13, pin12
  _74151 #(.VccGndPorts("true")) u_74151_2 (
    .pin3(AIN[2]), .pin4(AIN[0]), .pin5(SHIFTOUT[1]), .pin8(GND), .pin16(VCC), .pin11(S0),
    .pin10(n74151_1_pin10), .pin9(n74151_1_pin10));  // open: pin1, pin2, pin6, pin7, pin15, pin14, pin13, pin12
  _74151 #(.VccGndPorts("true")) u_74151_3 (
    .pin3(AIN[3]), .pin4(AIN[1]), .pin5(SHIFTOUT[2]), .pin8(GND), .pin16(VCC), .pin11(S0),
    .pin10(n74151_1_pin10), .pin9(n74151_1_pin10));  // open: pin1, pin2, pin6, pin7, pin15, pin14, pin13, pin12
  _74151 #(.VccGndPorts("true")) u_74151_4 (
    .pin3(AIN[4]), .pin4(AIN[2]), .pin5(SHIFTOUT[3]), .pin8(GND), .pin16(VCC), .pin11(S0),
    .pin10(n74151_1_pin10), .pin9(n74151_1_pin10));  // open: pin1, pin2, pin6, pin7, pin15, pin14, pin13, pin12
  _74151 #(.VccGndPorts("true")) u_74151_5 (
    .pin3(AIN[5]), .pin4(AIN[3]), .pin5(SHIFTOUT[4]), .pin8(GND), .pin16(VCC), .pin11(S0),
    .pin10(n74151_1_pin10), .pin9(n74151_1_pin10));  // open: pin1, pin2, pin6, pin7, pin15, pin14, pin13, pin12
  _74151 #(.VccGndPorts("true")) u_74151_6 (
    .pin3(AIN[6]), .pin4(AIN[4]), .pin5(SHIFTOUT[5]), .pin8(GND), .pin16(VCC), .pin11(S0),
    .pin10(n74151_1_pin10), .pin9(n74151_1_pin10));  // open: pin1, pin2, pin6, pin7, pin15, pin14, pin13, pin12
  _74151 #(.VccGndPorts("true")) u_74151_7 (
    .pin3(AIN[7]), .pin4(AIN[5]), .pin5(SHIFTOUT[6]), .pin8(GND), .pin16(VCC), .pin11(S0),
    .pin10(n74151_1_pin10), .pin9(n74151_1_pin10));  // open: pin1, pin2, pin6, pin7, pin15, pin14, pin13, pin12
  _74151 #(.VccGndPorts("true")) u_74151_8 (
    .pin3(AIN[8]), .pin4(AIN[6]), .pin5(SHIFTOUT[7]), .pin8(GND), .pin16(VCC), .pin11(S0),
    .pin10(n74151_1_pin10), .pin9(n74151_1_pin10));  // open: pin1, pin2, pin6, pin7, pin15, pin14, pin13, pin12
  _74151 #(.VccGndPorts("true")) u_74151_9 (
    .pin3(AIN[9]), .pin4(AIN[7]), .pin5(SHIFTOUT[8]), .pin8(GND), .pin16(VCC), .pin11(S0),
    .pin10(n74151_1_pin10), .pin9(n74151_1_pin10));  // open: pin1, pin2, pin6, pin7, pin15, pin14, pin13, pin12
  _74151 #(.VccGndPorts("true")) u_74151_10 (
    .pin3(AIN[10]), .pin4(AIN[8]), .pin5(SHIFTOUT[9]), .pin8(GND), .pin16(VCC), .pin11(S0),
    .pin10(n74151_1_pin10), .pin9(n74151_1_pin10));  // open: pin1, pin2, pin6, pin7, pin15, pin14, pin13, pin12
  _74151 #(.VccGndPorts("true")) u_74151_11 (
    .pin3(AIN[11]), .pin4(AIN[9]), .pin5(SHIFTOUT[10]), .pin8(GND), .pin16(VCC), .pin11(S0),
    .pin10(n74151_1_pin10), .pin9(n74151_1_pin10));  // open: pin1, pin2, pin6, pin7, pin15, pin14, pin13, pin12
  _74151 #(.VccGndPorts("true")) u_74151_12 (
    .pin3(AIN[12]), .pin4(AIN[10]), .pin5(SHIFTOUT[11]), .pin8(GND), .pin16(VCC), .pin11(S0),
    .pin10(n74151_1_pin10), .pin9(n74151_1_pin10));  // open: pin1, pin2, pin6, pin7, pin15, pin14, pin13, pin12
  _74151 #(.VccGndPorts("true")) u_74151_13 (
    .pin3(AIN[13]), .pin4(AIN[11]), .pin5(SHIFTOUT[12]), .pin8(GND), .pin16(VCC), .pin11(S0),
    .pin10(n74151_1_pin10), .pin9(n74151_1_pin10));  // open: pin1, pin2, pin6, pin7, pin15, pin14, pin13, pin12
  _74151 #(.VccGndPorts("true")) u_74151_14 (
    .pin3(AIN[14]), .pin4(AIN[12]), .pin5(SHIFTOUT[13]), .pin8(GND), .pin16(VCC), .pin11(S0),
    .pin10(n74151_1_pin10), .pin9(n74151_1_pin10));  // open: pin1, pin2, pin6, pin7, pin15, pin14, pin13, pin12
  _74151 #(.VccGndPorts("true")) u_74151_15 (
    .pin3(AIN[15]), .pin4(AIN[13]), .pin5(SHIFTOUT[14]), .pin8(GND), .pin16(VCC), .pin11(S0),
    .pin10(n74151_1_pin10), .pin9(n74151_1_pin10));  // open: pin1, pin2, pin6, pin7, pin15, pin14, pin13, pin12
  _74151 #(.VccGndPorts("true")) u_74151_16 (
    .pin3(MSBIN), .pin4(AIN[14]), .pin5(SHIFTOUT[15]), .pin8(GND), .pin16(VCC), .pin11(S0),
    .pin10(n74151_1_pin10), .pin9(n74151_1_pin10));  // open: pin1, pin2, pin6, pin7, pin15, pin14, pin13, pin12
  // also tied to GND on the sheet: n74151_1_pin10

  // Notes on the sheet:
  //   0
  //   1
  //   2
  //   3
  //   4
  //   5
  //   6
  //   7
  //   8
  //   9
  //   10
  //   11
  //   12
  //   13
  //   14
  //   15
  //   0-> shift to MSB
  //   1-> shift to LSB
  //   H0
  //   H1
  //   H2
  //   H3
  //   H4
  //   H5
  //   H6
  //   H7
  //   H8
  //   H9
  //   H10
  //   H11
  //   H12
  //   H13
  //   H14
  //   H15
endmodule

module ALSU (
  input  VCC,
  input  GND,
  input  S3,
  input  S2,
  input  S1,
  input  S0,
  input  CIN,
  input  [15:0] BIN,
  input  [15:0] AIN,
  input  LSBIN,
  input  MSBIN,
  output COUT,
  output [15:0] ALSUOUT
);

  wire and_1_out, and_2_out, and_3_out, and_4_out, not_1_out, not_2_out, not_3_out, not_4_out, or_1_out,
       or_2_out;
  wire [15:0] arithmaticcirc_1_outarith, logiccirc_1_outlogic, shiftcirc_1_shiftout;

  not not_1 (not_1_out, S1);
  not not_2 (not_2_out, S0);
  not not_3 (not_3_out, S1);
  not not_4 (not_4_out, S0);
  and and_1 (and_1_out, not_1_out, not_2_out);
  and and_2 (and_2_out, not_3_out, S0);
  and and_3 (and_3_out, S1, not_4_out);
  and and_4 (and_4_out, S1, S0);
  or or_1 (or_1_out, and_4_out, and_1_out);
  or or_2 (or_2_out, and_4_out, and_3_out);
  arithmaticCirc arithmaticcirc_1 (
    .GND(GND), .VCC(VCC), .AIN(AIN), .BIN(BIN), .S1(or_1_out), .S0(or_2_out), .CIN(CIN),
    .OUTARITH(arithmaticcirc_1_outarith), .COUT(COUT));
  logicCirc logiccirc_1 (
    .VCC(VCC), .BIN(BIN), .ENActiveHigh(VCC), .AIN(AIN), .S0(S0), .S1(S1), .GND(GND),
    .OUTLOGIC(logiccirc_1_outlogic));
  shiftCirc shiftcirc_1 (
    .VCC(VCC), .GND(GND), .S0(S2), .LSBIN(LSBIN), .MSBIN(MSBIN), .AIN(AIN), .SHIFTOUT(shiftcirc_1_shiftout));
  sixteenFourToOneMultiplexer sixteenfourtoonemultiplexer_1 (
    .ENActiveHigh(VCC), .GND(GND), .VCC(VCC), .S0(S2), .S1(S3), .INPUT0(arithmaticcirc_1_outarith),
    .INPUT1(logiccirc_1_outlogic), .INPUT2(shiftcirc_1_shiftout), .INPUT3(shiftcirc_1_shiftout),
    .DATAOUT(ALSUOUT));

  // Notes on the sheet:
  //   S1
  //   S0
  //   To make it compaltible with the table in moris mano book
  //   S1
  //   S0
  //   S3
  //   S2
endmodule
// CU
module controlUnit (
  input  CLK,
  input  VCC,
  input  GND,
  input  [15:0] irIN,
  input  bit12AR,
  input  [15:0] ACIN,
  input  [15:0] DRIN,
  input  scCLR,
  input  EFLIPFLOPIN,
  input  inputBufferNotEmpty,
  output BS3,
  output BS2,
  output BS1,
  output BS0,
  output ARLD,
  output ROMREAD,
  output ROMWRITE,
  output RAMREAD,
  output RAMWRITE,
  output IRLD,
  output ACCLR,
  output ECLR,
  output PCINCR,
  output ACCMPLMNT,
  output ECMPLMNT,
  output ACSHFR,
  output ACSHFL,
  output ACLOAD,
  output ELOAD,
  output DRLOAD,
  output ALSUS3,
  output ALSUS2,
  output ALSUS1,
  output ALSUS0,
  output MLTDRINRIN,
  output PCLOAD,
  output ARINCR,
  output DRINCR,
  output OUTRLOAD,
  output [3:0] sequencer,
  output ALSUSELECTOR,
  output ACINCR,
  output TRLOAD,
  output inputFlush,
  output LOADB1,
  output LOADB2,
  output LOADB3,
  output LOADB4,
  output LOADB5,
  output LOADB6,
  output LOADB7,
  output LOADB8,
  output LOADB9,
  output LOADB10,
  output LOADB11,
  output LOADB12,
  output LOADB13,
  output LOADB14,
  output LOADB15
);

  wire acLOAD3, acLOAD4, acLOAD5, acLOAD6, acLOAD7, alsuINSELECTOR, alsuINSELECTOR2, alsuINSELECTOR3,
       and_1_out, and_2_out, and_5_out, and_7_out, and_9_out, and_14_out, and_22_out, and_23_out, and_24_out,
       and_25_out, and_36_out, and_37_out, and_38_out, and_39_out, and_40_out, and_62_out, and_74_out,
       and_75_out, and_83_out, and_84_out, arINCR_t, arLOAD, arLOAD2, arLoad3, arLoad4, button_1_out,
       button_2_out, clock_1_out, D0, D1, D2, D3, D4, D5, D6, D7, decoder_1_out0, dFGO, dFLIPS, dIEN,
       drLOAD1, drLOAD_t, fgiOUT, FGOLOAD, fgoOUT, flipS, flipsCLR, flipsLOAD, IENCLR, IENCLR1, IENOUT,
       n7404_1_pin1, n7404_1_pin3, n7404_1_pin5, n7404_1_pin9, n7404_1_pin11, n7404_1_pin13, n7404_2_pin1,
       n7404_2_pin3, n7404_2_pin5, n7404_2_pin9, n7404_2_pin11, n7404_2_pin13, n7404_4_pin6, n7404_4_pin9,
       n7404_4_pin11, n7404_4_pin13, n74138_1_pin7, n74138_1_pin9, n74138_2_pin7, n74138_2_pin9,
       n74138_3_pin7, n74138_3_pin9, n74138_3_pin10, n74138_3_pin11, n74138_3_pin12, n74163_1_pin1,
       n74175_1_pin1, n74175_1_pin9, n74175_2_pin1, n74175_2_pin9, n74175_3_pin3, n74175_3_pin9,
       n74175_4_pin2, n74175_5_pin9, n74175_6_pin1, n74175_6_pin9, n74175_7_pin1, n74175_7_pin9, not_3_out,
       not_4_out, not_5_out, not_6_out, not_7_out, not_8_out, not_9_out, not_10_out, not_11_out, not_12_out,
       not_13_out, not_14_out, not_15_out, not_16_out, not_17_out, not_18_out, not_19_out, not_20_out,
       not_21_out, not_22_out, not_23_out, not_24_out, not_25_out, not_26_out, not_27_out, not_28_out,
       not_29_out, not_30_out, not_31_out, not_32_out, not_33_out, not_34_out, not_35_out, not_36_out,
       not_37_out, not_38_out, not_39_out, not_40_out, not_41_out, not_42_out, not_43_out, not_44_out,
       not_45_out, not_46_out, not_47_out, not_48_out, not_49_out, not_50_out, not_51_out, not_52_out,
       not_53_out, not_54_out, not_55_out, not_56_out, not_57_out, not_58_out, not_59_out, not_60_out,
       not_61_out, not_62_out, not_63_out, not_64_out, not_65_out, not_66_out, not_67_out, not_68_out,
       not_69_out, not_70_out, not_71_out, not_72_out, not_73_out, not_74_out, not_75_out, not_76_out,
       not_77_out, not_78_out, not_79_out, not_80_out, not_81_out, not_82_out, not_83_out, not_84_out,
       not_85_out, not_86_out, not_87_out, not_88_out, not_89_out, not_90_out, not_91_out, not_92_out,
       not_93_out, not_94_out, not_95_out, not_96_out, not_97_out, not_98_out, not_99_out, not_100_out,
       not_101_out, not_102_out, not_103_out, not_104_out, not_105_out, not_106_out, not_107_out,
       not_108_out, not_109_out, not_110_out, not_111_out, not_112_out, not_113_out, not_114_out,
       not_115_out, not_116_out, not_117_out, not_118_out, not_119_out, not_120_out, not_121_out,
       not_122_out, not_123_out, not_124_out, not_125_out, not_126_out, not_127_out, not_128_out,
       not_129_out, not_130_out, not_131_out, not_132_out, not_133_out, not_134_out, not_135_out,
       not_136_out, not_137_out, not_138_out, not_139_out, not_140_out, not_141_out, not_142_out,
       not_143_out, not_144_out, not_145_out, not_146_out, not_147_out, not_148_out, not_149_out,
       not_150_out, not_151_out, not_152_out, not_153_out, not_154_out, not_155_out, not_156_out,
       not_157_out, not_158_out, not_159_out, not_160_out, not_161_out, not_162_out, not_163_out,
       not_164_out, not_165_out, not_166_out, not_167_out, not_168_out, not_169_out, not_170_out,
       not_171_out, not_172_out, not_173_out, not_174_out, not_175_out, not_176_out, not_177_out,
       not_178_out, not_179_out, not_180_out, not_181_out, not_182_out, not_183_out, not_184_out,
       not_185_out, not_186_out, not_187_out, not_188_out, not_189_out, not_190_out, not_191_out,
       not_192_out, not_193_out, not_194_out, not_195_out, not_196_out, not_197_out, not_198_out,
       not_199_out, not_200_out, not_201_out, not_202_out, not_203_out, not_204_out, not_205_out,
       not_206_out, not_207_out, not_208_out, not_209_out, not_210_out, not_211_out, not_212_out,
       not_213_out, not_214_out, not_215_out, not_216_out, not_217_out, not_218_out, not_219_out,
       not_220_out, not_221_out, not_222_out, not_223_out, not_224_out, not_225_out, not_226_out,
       not_227_out, not_228_out, not_229_out, not_230_out, not_231_out, not_232_out, not_233_out,
       not_234_out, not_235_out, not_236_out, not_237_out, not_238_out, not_239_out, not_240_out,
       not_241_out, not_242_out, not_243_out, not_244_out, not_245_out, not_246_out, not_247_out,
       not_248_out, not_249_out, not_250_out, not_251_out, not_252_out, not_253_out, not_256_out, or_22_out,
       or_24_out, or_25_out, or_26_out, or_28_out, or_29_out, or_30_out, or_32_out, or_33_out, or_34_out,
       or_35_out, pcINCR1, pcINCR2, pcINCR3, pcINCR4, pcINCR5, pcINCR7, pcLOAD1, pcLOAD2, pcLOAD_t, ramRead1,
       ramRead2, ramRead_t, ramWrite1, ramWrite2, ramWrite3, ramWrite_t, romRead1, romRead2, romRead_t,
       romWrite1, romWrite2, romWrite3, romWrite_t, ROUT, S05, S07, S17, S18, S24, S25, S28, S33, scCLR1,
       scCLR2, scCLR3, scCLR_t, T0, T1, T2, T3, T4, T5, T6, T7, T8;
  wire [3:0] and_70_out;
  wire [7:0] n7404_1_pin2;
  wire [15:9] n7404_2_pin4;

  or or_1 (BS1, S17, arINCR_t, ramRead2, ramRead_t, TRLOAD, ramRead1, arLOAD, S05, S18);
  or or_2 (BS3, S33, romRead2, arLoad4, romRead_t, romRead1, pcLOAD_t);
  or or_3 (BS2, S28, S25, ramRead2, ramRead_t, S24, arLOAD2, ramRead1, OUTRLOAD, S18);
  or or_4 (BS0, pcLOAD2, S05, ramRead2, ramRead_t, pcLOAD1, arLOAD2, ramRead1, S07, arLoad4, pcLOAD_t);
  or or_5 (ARLD, arLOAD, arLoad3, arLoad4, arLOAD2);
  or or_6 (ALSUSELECTOR, alsuINSELECTOR, alsuINSELECTOR3, alsuINSELECTOR2);
  or or_7 (PCINCR, IENCLR1, pcINCR7, pcINCR1, pcINCR2, pcINCR3, pcINCR4, pcINCR5, IRLD);
  or or_8 (ACLOAD, acLOAD5, ACCMPLMNT, ACSHFR, acLOAD4, ACSHFL, acLOAD3, acLOAD6, acLOAD7);
  or or_9 (ELOAD, ECMPLMNT, acLOAD4);
  or or_10 (DRLOAD, drLOAD_t, drLOAD1);
  or or_11 (ALSUS3, ACSHFR, ACSHFL);
  or or_12 (ALSUS2, acLOAD3, ACSHFL, ACCMPLMNT);
  or or_13 (ALSUS1, ACCMPLMNT, 1'b0);
  or or_14 (ALSUS0, acLOAD4, ACCMPLMNT);
  or or_15 (MLTDRINRIN, acLOAD3, acLOAD3, acLOAD7, acLOAD6, acLOAD4);
  or or_16 (PCLOAD, pcLOAD_t, pcLOAD2, pcLOAD1);
  or or_17 (ROMREAD, romRead_t, romRead1, romRead2);
  or or_18 (ROMWRITE, romWrite_t, romWrite2, romWrite3, romWrite1);
  or or_19 (ARINCR, arINCR_t, arINCR_t);
  or or_20 (RAMREAD, ramRead_t, ramRead1, ramRead2);
  or or_21 (RAMWRITE, ramWrite_t, ramWrite2, ramWrite3, ramWrite1);
  Clock clock_1 (.out(clock_1_out));
  Button button_1 (.out(button_1_out));
  or or_22 (or_22_out, scCLR, button_2_out, button_1_out);
  or or_23 (dFLIPS, acLOAD7, scCLR, button_1_out, scCLR_t, scCLR2, button_2_out, scCLR3, scCLR1, alsuINSELECTOR2, button_2_out, IENCLR1);
  and and_1 (and_1_out, CLK, flipS);
  or or_24 (or_24_out, and_1_out, and_2_out);
  and and_2 (and_2_out, CLK, or_22_out);
  _7404 #(.VccGndPorts("true")) u_7404_1 (
    .pin1(n7404_1_pin1), .pin2(n7404_1_pin2[0]), .pin3(n7404_1_pin3), .pin4(n7404_1_pin2[1]),
    .pin5(n7404_1_pin5), .pin6(n7404_1_pin2[2]), .pin7(GND), .pin14(VCC), .pin13(n7404_1_pin13),
    .pin12(n7404_1_pin2[3]), .pin11(n7404_1_pin11), .pin10(n7404_1_pin2[4]), .pin9(n7404_1_pin9),
    .pin8(n7404_1_pin2[5]));
  _74138 #(.VccGndPorts("true")) u_74138_1 (
    .pin1(irIN[12]), .pin2(irIN[13]), .pin3(irIN[14]), .pin4(GND), .pin5(GND), .pin6(VCC),
    .pin7(n74138_1_pin7), .pin8(GND), .pin16(VCC), .pin15(n7404_1_pin1), .pin14(n7404_1_pin3),
    .pin13(n7404_1_pin5), .pin12(n7404_1_pin13), .pin11(n7404_1_pin11), .pin10(n7404_1_pin9),
    .pin9(n74138_1_pin9));
  _7404 #(.VccGndPorts("true")) u_7404_2 (
    .pin1(n7404_2_pin1), .pin2(T8), .pin3(n7404_2_pin3), .pin4(n7404_2_pin4[9]), .pin5(n7404_2_pin5),
    .pin6(n7404_2_pin4[10]), .pin7(GND), .pin14(VCC), .pin13(n7404_2_pin13), .pin12(n7404_2_pin4[11]),
    .pin11(n7404_2_pin11), .pin10(n7404_2_pin4[12]), .pin9(n7404_2_pin9), .pin8(n7404_2_pin4[13]));
  _74138 #(.VccGndPorts("true")) u_74138_2 (
    .pin1(sequencer[0]), .pin2(sequencer[1]), .pin3(sequencer[2]), .pin4(GND), .pin5(GND),
    .pin6(sequencer[3]), .pin7(n74138_2_pin7), .pin8(GND), .pin16(VCC), .pin15(n7404_2_pin1),
    .pin14(n7404_2_pin3), .pin13(n7404_2_pin5), .pin12(n7404_2_pin13), .pin11(n7404_2_pin11),
    .pin10(n7404_2_pin9), .pin9(n74138_2_pin9));
  _74163 #(.VccGndPorts("true")) u_74163_1 (
    .pin1(n74163_1_pin1), .pin2(or_24_out), .pin7(VCC), .pin8(GND), .pin16(VCC), .pin14(sequencer[0]),
    .pin13(sequencer[1]), .pin12(sequencer[2]), .pin11(sequencer[3]), .pin10(VCC));  // open: pin3, pin4, pin5, pin6, pin15, pin9
  _7404 #(.VccGndPorts("true")) u_7404_3 (
    .pin7(GND), .pin14(VCC), .pin13(n74138_1_pin9), .pin12(n7404_1_pin2[6]), .pin11(n74138_1_pin7),
    .pin10(n7404_1_pin2[7]));  // open: pin1, pin2, pin3, pin4, pin5, pin6, pin9, pin8
  _7404 #(.VccGndPorts("true")) u_7404_4 (
    .pin1(n74138_2_pin9), .pin2(n7404_2_pin4[14]), .pin3(n74138_2_pin7), .pin4(n7404_2_pin4[15]),
    .pin5(sequencer[3]), .pin6(n7404_4_pin6), .pin7(GND), .pin14(VCC), .pin13(n7404_4_pin13), .pin12(T0),
    .pin11(n7404_4_pin11), .pin10(T1), .pin9(n7404_4_pin9), .pin8(T2));
  _74138 #(.VccGndPorts("true")) u_74138_3 (
    .pin1(sequencer[0]), .pin2(sequencer[1]), .pin3(sequencer[2]), .pin4(GND), .pin5(GND),
    .pin6(n7404_4_pin6), .pin7(n74138_3_pin7), .pin8(GND), .pin16(VCC), .pin15(n7404_4_pin13),
    .pin14(n7404_4_pin11), .pin13(n7404_4_pin9), .pin12(n74138_3_pin12), .pin11(n74138_3_pin11),
    .pin10(n74138_3_pin10), .pin9(n74138_3_pin9));
  LED led_1 (.in(sequencer[3]));
  eightBitLoad eightbitload_1 (
    .LoadActiveHigh(arLOAD2), .VCC(VCC), .GND(GND), .CLK(CLK), .BitsIN(n7404_1_pin2),
    .BitsOUT({D7, D6, D5, D4, D3, D2, D1, D0}));  // open: ClearActiveLow, cascadeOut
  LedBar #(.matrixcols(3)) ledbar_1 (.led0(sequencer[0]), .led1(sequencer[1]), .led2(sequencer[2]));
  _7404 #(.VccGndPorts("true")) u_7404_5 (
    .pin1(n74138_3_pin12), .pin2(T3), .pin3(n74138_3_pin11), .pin4(T4), .pin5(n74138_3_pin10), .pin6(T5),
    .pin7(GND), .pin14(VCC), .pin13(n74138_3_pin9), .pin12(T6), .pin11(n74138_3_pin7), .pin10(T7),
    .pin9(dFLIPS), .pin8(n74163_1_pin1));
  _74175 #(.VccGndPorts("true")) u_74175_1 (
    .pin1(n74175_1_pin1), .pin4(irIN[15]), .pin8(GND), .pin16(VCC), .pin9(n74175_1_pin9));  // open: pin2, pin3, pin5, pin6, pin7, pin15, pin14, pin13, pin12, pin11, pin10
  and and_3 (n74175_1_pin9, arLOAD2, CLK);
  not not_1 (n74175_1_pin1, GND);
  _74175 #(.VccGndPorts("true")) u_74175_2 (
    .pin1(n74175_2_pin1), .pin2(flipS), .pin3(flipsLOAD), .pin4(dFLIPS), .pin8(GND), .pin16(VCC),
    .pin9(n74175_2_pin9));  // open: pin5, pin6, pin7, pin15, pin14, pin13, pin12, pin11, pin10
  and and_4 (n74175_2_pin9, flipsLOAD, CLK);
  not not_2 (n74175_2_pin1, flipsCLR);
  or or_25 (or_25_out, fgoOUT, fgiOUT);
  not not_3 (not_3_out, T3);
  not not_4 (not_4_out, T0);
  not not_5 (not_5_out, T1);
  not not_6 (not_6_out, T2);
  not not_7 (not_7_out, T4);
  and and_5 (and_5_out, not_3_out, not_4_out, not_5_out, not_6_out, IENOUT, or_25_out, not_7_out);
  _74175 #(.VccGndPorts("true")) u_74175_3 (
    .pin2(ROUT), .pin3(n74175_3_pin3), .pin4(and_5_out), .pin8(GND), .pin16(VCC), .pin9(n74175_3_pin9));  // open: pin1, pin5, pin6, pin7, pin15, pin14, pin13, pin12, pin11, pin10
  and and_6 (n74175_3_pin9, or_26_out, CLK);
  not not_8 (not_8_out, ROUT);
  or or_26 (or_26_out, not_8_out, n74175_4_pin2);
  _74175 #(.VccGndPorts("true")) u_74175_4 (
    .pin2(n74175_4_pin2), .pin4(IENCLR1), .pin8(GND), .pin16(VCC), .pin9(CLK));  // open: pin1, pin3, pin5, pin6, pin7, pin15, pin14, pin13, pin12, pin11, pin10
  Button button_2 (.out(button_2_out));
  not not_9 (not_9_out, irIN[15]);
  not not_10 (not_10_out, D7);
  and and_7 (and_7_out, n74175_3_pin3, D7);
  not not_11 (not_11_out, irIN[4]);
  not not_12 (not_12_out, irIN[3]);
  not not_13 (not_13_out, irIN[2]);
  not not_14 (not_14_out, irIN[1]);
  not not_15 (not_15_out, irIN[0]);
  not not_16 (not_16_out, irIN[4]);
  not not_17 (not_17_out, irIN[3]);
  not not_18 (not_18_out, irIN[2]);
  not not_19 (not_19_out, irIN[1]);
  not not_20 (not_20_out, irIN[0]);
  not not_21 (not_21_out, irIN[4]);
  not not_22 (not_22_out, irIN[3]);
  not not_23 (not_23_out, irIN[2]);
  not not_24 (not_24_out, irIN[1]);
  not not_25 (not_25_out, irIN[0]);
  not not_26 (not_26_out, irIN[4]);
  not not_27 (not_27_out, irIN[3]);
  not not_28 (not_28_out, irIN[2]);
  not not_29 (not_29_out, irIN[1]);
  not not_30 (not_30_out, irIN[0]);
  not not_31 (not_31_out, irIN[4]);
  not not_32 (not_32_out, irIN[3]);
  not not_33 (not_33_out, irIN[2]);
  not not_34 (not_34_out, irIN[1]);
  not not_35 (not_35_out, irIN[0]);
  not not_36 (not_36_out, irIN[4]);
  not not_37 (not_37_out, irIN[3]);
  not not_38 (not_38_out, irIN[2]);
  not not_39 (not_39_out, irIN[1]);
  not not_40 (not_40_out, irIN[0]);
  not not_41 (not_41_out, irIN[4]);
  not not_42 (not_42_out, irIN[3]);
  not not_43 (not_43_out, irIN[2]);
  not not_44 (not_44_out, irIN[1]);
  not not_45 (not_45_out, irIN[0]);
  not not_46 (not_46_out, irIN[3]);
  not not_47 (not_47_out, irIN[2]);
  not not_48 (not_48_out, irIN[1]);
  not not_49 (not_49_out, irIN[0]);
  not not_50 (not_50_out, irIN[2]);
  not not_51 (not_51_out, irIN[1]);
  not not_52 (not_52_out, irIN[0]);
  not not_53 (not_53_out, irIN[1]);
  not not_54 (not_54_out, irIN[0]);
  not not_55 (not_55_out, irIN[0]);
  and and_8 (alsuINSELECTOR, n74175_3_pin3, not_10_out);
  and and_9 (and_9_out, and_7_out, not_9_out, T3);
  not not_56 (not_56_out, irIN[10]);
  not not_57 (not_57_out, irIN[9]);
  not not_58 (not_58_out, irIN[8]);
  not not_59 (not_59_out, irIN[7]);
  not not_60 (not_60_out, irIN[6]);
  not not_61 (not_61_out, irIN[5]);
  not not_62 (not_62_out, irIN[11]);
  not not_63 (not_63_out, irIN[9]);
  not not_64 (not_64_out, irIN[8]);
  not not_65 (not_65_out, irIN[7]);
  not not_66 (not_66_out, irIN[6]);
  not not_67 (not_67_out, irIN[5]);
  not not_68 (not_68_out, irIN[11]);
  not not_69 (not_69_out, irIN[10]);
  not not_70 (not_70_out, irIN[8]);
  not not_71 (not_71_out, irIN[7]);
  not not_72 (not_72_out, irIN[6]);
  not not_73 (not_73_out, irIN[5]);
  not not_74 (not_74_out, irIN[11]);
  not not_75 (not_75_out, irIN[10]);
  not not_76 (not_76_out, irIN[9]);
  not not_77 (not_77_out, irIN[7]);
  not not_78 (not_78_out, irIN[6]);
  not not_79 (not_79_out, irIN[5]);
  not not_80 (not_80_out, irIN[11]);
  not not_81 (not_81_out, irIN[10]);
  not not_82 (not_82_out, irIN[9]);
  not not_83 (not_83_out, irIN[8]);
  not not_84 (not_84_out, irIN[6]);
  not not_85 (not_85_out, irIN[5]);
  not not_86 (not_86_out, irIN[11]);
  not not_87 (not_87_out, irIN[10]);
  not not_88 (not_88_out, irIN[9]);
  not not_89 (not_89_out, irIN[8]);
  not not_90 (not_90_out, irIN[7]);
  not not_91 (not_91_out, irIN[5]);
  not not_92 (not_92_out, irIN[11]);
  not not_93 (not_93_out, irIN[10]);
  not not_94 (not_94_out, irIN[9]);
  not not_95 (not_95_out, irIN[8]);
  not not_96 (not_96_out, irIN[7]);
  not not_97 (not_97_out, irIN[6]);
  not not_98 (not_98_out, irIN[11]);
  not not_99 (not_99_out, irIN[10]);
  not not_100 (not_100_out, irIN[9]);
  not not_101 (not_101_out, irIN[8]);
  not not_102 (not_102_out, irIN[7]);
  not not_103 (not_103_out, irIN[6]);
  not not_104 (not_104_out, irIN[5]);
  not not_105 (not_105_out, irIN[11]);
  not not_106 (not_106_out, irIN[10]);
  not not_107 (not_107_out, irIN[9]);
  not not_108 (not_108_out, irIN[8]);
  not not_109 (not_109_out, irIN[7]);
  not not_110 (not_110_out, irIN[6]);
  not not_111 (not_111_out, irIN[5]);
  not not_112 (not_112_out, irIN[4]);
  not not_113 (not_113_out, irIN[11]);
  not not_114 (not_114_out, irIN[10]);
  not not_115 (not_115_out, irIN[9]);
  not not_116 (not_116_out, irIN[8]);
  not not_117 (not_117_out, irIN[7]);
  not not_118 (not_118_out, irIN[6]);
  not not_119 (not_119_out, irIN[5]);
  not not_120 (not_120_out, irIN[4]);
  not not_121 (not_121_out, irIN[3]);
  not not_122 (not_122_out, irIN[11]);
  not not_123 (not_123_out, irIN[10]);
  not not_124 (not_124_out, irIN[9]);
  not not_125 (not_125_out, irIN[8]);
  not not_126 (not_126_out, irIN[7]);
  not not_127 (not_127_out, irIN[6]);
  not not_128 (not_128_out, irIN[5]);
  not not_129 (not_129_out, irIN[4]);
  not not_130 (not_130_out, irIN[3]);
  not not_131 (not_131_out, irIN[2]);
  not not_132 (not_132_out, irIN[11]);
  not not_133 (not_133_out, irIN[10]);
  not not_134 (not_134_out, irIN[9]);
  not not_135 (not_135_out, irIN[8]);
  not not_136 (not_136_out, irIN[7]);
  not not_137 (not_137_out, irIN[6]);
  not not_138 (not_138_out, irIN[5]);
  not not_139 (not_139_out, irIN[4]);
  not not_140 (not_140_out, irIN[3]);
  not not_141 (not_141_out, irIN[2]);
  not not_142 (not_142_out, irIN[1]);
  not not_143 (not_143_out, irIN[15]);
  and and_10 (arLOAD, n74175_3_pin3, T0);
  and and_11 (arLOAD2, n74175_3_pin3, T2);
  and and_12 (IRLD, n74175_3_pin3, T1);
  not not_144 (not_144_out, bit12AR);
  and and_13 (arLoad3, alsuINSELECTOR, T3, irIN[15]);
  and and_14 (and_14_out, alsuINSELECTOR, T3, not_143_out);
  and and_15 (ACCLR, and_9_out, irIN[11], not_56_out, not_57_out, not_58_out, not_59_out, not_60_out, not_61_out, not_11_out, not_12_out, not_13_out, not_14_out, not_15_out);
  and and_16 (ECLR, and_9_out, not_62_out, irIN[10], not_63_out, not_64_out, not_65_out, not_66_out, not_67_out, not_16_out, not_17_out, not_18_out, not_19_out, not_20_out);
  and and_17 (ACCMPLMNT, and_9_out, not_68_out, not_69_out, irIN[9], not_70_out, not_71_out, not_72_out, not_73_out, not_21_out, not_22_out, not_23_out, not_24_out, not_25_out);
  and and_18 (ECMPLMNT, and_9_out, not_74_out, not_75_out, not_76_out, irIN[8], not_77_out, not_78_out, not_79_out, not_26_out, not_27_out, not_28_out, not_29_out, not_30_out);
  and and_19 (ACSHFL, and_9_out, not_80_out, not_81_out, not_82_out, not_83_out, irIN[7], not_84_out, not_85_out, not_31_out, not_32_out, not_33_out, not_34_out, not_35_out);
  and and_20 (ACSHFR, and_9_out, not_86_out, not_87_out, not_88_out, not_89_out, not_90_out, irIN[6], not_91_out, not_36_out, not_37_out, not_38_out, not_39_out, not_40_out);
  and and_21 (ACINCR, and_9_out, not_92_out, not_93_out, not_94_out, not_95_out, not_96_out, not_97_out, irIN[5], not_41_out, not_42_out, not_43_out, not_44_out, not_45_out);
  and and_22 (and_22_out, and_9_out, not_98_out, not_99_out, not_100_out, not_101_out, not_102_out, not_103_out, not_104_out, irIN[4], not_46_out, not_47_out, not_48_out, not_49_out);
  and and_23 (and_23_out, and_9_out, not_105_out, not_106_out, not_107_out, not_108_out, not_109_out, not_110_out, not_111_out, not_112_out, irIN[3], not_50_out, not_51_out, not_52_out);
  and and_24 (and_24_out, and_9_out, not_113_out, not_114_out, not_115_out, not_116_out, not_117_out, not_118_out, not_119_out, not_120_out, not_121_out, irIN[2], not_53_out, not_54_out);
  and and_25 (and_25_out, and_9_out, not_122_out, not_123_out, not_124_out, not_125_out, not_126_out, not_127_out, not_128_out, not_129_out, not_130_out, not_131_out, irIN[1], not_55_out);
  and and_26 (flipsCLR, and_9_out, not_132_out, not_133_out, not_134_out, not_135_out, not_136_out, not_137_out, not_138_out, not_139_out, not_140_out, not_141_out, not_142_out, irIN[0]);
  and and_27 (romRead1, IRLD, not_144_out);
  and and_28 (ramRead1, IRLD, bit12AR);
  not not_145 (not_145_out, bit12AR);
  and and_29 (romRead_t, arLoad3, not_145_out);
  not not_146 (not_146_out, EFLIPFLOPIN);
  and and_30 (ramRead_t, arLoad3, bit12AR);
  and and_31 (pcINCR7, not_146_out, and_25_out);
  not not_147 (not_147_out, ACIN[15]);
  and and_32 (pcINCR1, not_147_out, and_22_out);
  and and_33 (pcINCR2, ACIN[15], and_23_out);
  and and_34 (pcINCR3, and_36_out, and_24_out);
  and and_35 (scCLR1, and_7_out, T5);
  not not_148 (not_148_out, ACIN[15]);
  not not_149 (not_149_out, ACIN[14]);
  not not_150 (not_150_out, ACIN[13]);
  not not_151 (not_151_out, ACIN[12]);
  not not_152 (not_152_out, ACIN[11]);
  not not_153 (not_153_out, ACIN[10]);
  not not_154 (not_154_out, ACIN[9]);
  not not_155 (not_155_out, ACIN[8]);
  not not_156 (not_156_out, ACIN[7]);
  not not_157 (not_157_out, ACIN[6]);
  and and_36 (and_36_out, not_148_out, not_149_out, not_150_out, not_151_out, not_152_out, not_153_out, not_154_out, not_155_out, not_157_out, not_158_out, not_159_out, not_160_out, not_161_out, not_162_out, not_163_out, not_156_out);
  not not_158 (not_158_out, ACIN[5]);
  not not_159 (not_159_out, ACIN[4]);
  not not_160 (not_160_out, ACIN[3]);
  not not_161 (not_161_out, ACIN[2]);
  not not_162 (not_162_out, ACIN[1]);
  not not_163 (not_163_out, ACIN[0]);
  and and_37 (and_37_out, D0, T4);
  and and_38 (and_38_out, D1, T4);
  and and_39 (and_39_out, D2, T4);
  and and_40 (and_40_out, D6, T4);
  or or_27 (drLOAD_t, and_37_out, and_38_out, and_39_out, and_40_out);
  not not_164 (not_164_out, bit12AR);
  and and_41 (romRead2, drLOAD_t, not_164_out);
  and and_42 (ramRead2, drLOAD_t, bit12AR);
  or or_28 (or_28_out, D0, D1, D1, D5, D2);
  and and_43 (acLOAD3, D0, T5);
  and and_44 (scCLR_t, or_28_out, T5);
  and and_45 (acLOAD4, D1, T5);
  and and_46 (acLOAD6, D2, T5);
  or or_29 (or_29_out, D3, D4);
  and and_47 (S24, D3, T4);
  and and_48 (scCLR2, or_29_out, T4);
  and and_49 (pcLOAD2, D4, T4);
  and and_50 (arINCR_t, D5, T4);
  not not_165 (not_165_out, bit12AR);
  and and_51 (pcLOAD1, D5, T5);
  not not_166 (not_166_out, bit12AR);
  and and_52 (romWrite1, arINCR_t, not_165_out);
  and and_53 (ramWrite1, arINCR_t, bit12AR);
  and and_54 (romWrite2, S24, not_166_out);
  and and_55 (ramWrite2, S24, bit12AR);
  and and_56 (DRINCR, D6, T5);
  and and_57 (S05, D6, T6);
  not not_167 (not_167_out, bit12AR);
  and and_58 (scCLR3, D6, T6);
  and and_59 (romWrite_t, S05, not_167_out);
  and and_60 (ramWrite_t, S05, bit12AR);
  and and_61 (pcINCR4, and_62_out, S05);
  not not_168 (not_168_out, DRIN[15]);
  not not_169 (not_169_out, DRIN[14]);
  not not_170 (not_170_out, DRIN[13]);
  not not_171 (not_171_out, DRIN[12]);
  not not_172 (not_172_out, DRIN[11]);
  not not_173 (not_173_out, DRIN[10]);
  not not_174 (not_174_out, DRIN[9]);
  not not_175 (not_175_out, DRIN[8]);
  not not_176 (not_176_out, DRIN[6]);
  not not_177 (not_177_out, DRIN[5]);
  and and_62 (and_62_out, not_168_out, not_169_out, not_170_out, not_171_out, not_172_out, not_173_out, not_174_out, not_175_out, not_176_out, not_177_out, not_178_out, not_179_out, not_180_out, not_181_out, not_182_out, not_183_out);
  not not_178 (not_178_out, DRIN[4]);
  not not_179 (not_179_out, DRIN[3]);
  not not_180 (not_180_out, DRIN[2]);
  not not_181 (not_181_out, DRIN[1]);
  not not_182 (not_182_out, DRIN[0]);
  not not_183 (not_183_out, DRIN[7]);
  not not_184 (not_184_out, ROUT);
  and and_63 (alsuINSELECTOR3, not_184_out, irIN[15], irIN[11], irIN[10], irIN[9], irIN[8], irIN[7], irIN[6], irIN[5], irIN[4], D7);
  not not_185 (not_185_out, alsuINSELECTOR3);
  and and_64 (alsuINSELECTOR2, D7, not_184_out, T3, not_185_out, irIN[15]);
  or or_30 (or_30_out, IENCLR1, IENCLR);
  not not_186 (not_186_out, or_30_out);
  _74175 #(.VccGndPorts("true")) u_74175_5 (
    .pin1(not_186_out), .pin2(IENOUT), .pin4(dIEN), .pin8(GND), .pin16(VCC), .pin9(n74175_5_pin9));  // open: pin3, pin5, pin6, pin7, pin15, pin14, pin13, pin12, pin11, pin10
  and and_65 (acLOAD7, alsuINSELECTOR3, T4);
  and and_66 (n74175_5_pin9, dIEN, CLK);
  and and_67 (and_70_out[3], irIN[3], S28);
  and and_68 (and_70_out[2], irIN[2], S28);
  and and_69 (and_70_out[1], irIN[1], S28);
  and and_70 (and_70_out[0], irIN[0], S28);
  and and_71 (drLOAD1, alsuINSELECTOR3, T3);
  not not_187 (not_187_out, irIN[10]);
  not not_188 (not_188_out, irIN[9]);
  not not_189 (not_189_out, irIN[8]);
  not not_190 (not_190_out, irIN[7]);
  not not_191 (not_191_out, irIN[6]);
  not not_192 (not_192_out, irIN[5]);
  not not_193 (not_193_out, irIN[4]);
  not not_194 (not_194_out, irIN[3]);
  not not_195 (not_195_out, irIN[2]);
  not not_196 (not_196_out, irIN[1]);
  not not_197 (not_197_out, irIN[0]);
  not not_198 (not_198_out, irIN[11]);
  not not_199 (not_199_out, irIN[9]);
  not not_200 (not_200_out, irIN[8]);
  not not_201 (not_201_out, irIN[7]);
  not not_202 (not_202_out, irIN[6]);
  not not_203 (not_203_out, irIN[5]);
  not not_204 (not_204_out, irIN[4]);
  not not_205 (not_205_out, irIN[3]);
  not not_206 (not_206_out, irIN[2]);
  not not_207 (not_207_out, irIN[1]);
  not not_208 (not_208_out, irIN[0]);
  not not_209 (not_209_out, irIN[11]);
  not not_210 (not_210_out, irIN[10]);
  not not_211 (not_211_out, irIN[8]);
  not not_212 (not_212_out, irIN[7]);
  not not_213 (not_213_out, irIN[6]);
  not not_214 (not_214_out, irIN[5]);
  not not_215 (not_215_out, irIN[4]);
  not not_216 (not_216_out, irIN[3]);
  not not_217 (not_217_out, irIN[2]);
  not not_218 (not_218_out, irIN[1]);
  not not_219 (not_219_out, irIN[0]);
  not not_220 (not_220_out, irIN[11]);
  not not_221 (not_221_out, irIN[10]);
  not not_222 (not_222_out, irIN[9]);
  not not_223 (not_223_out, irIN[7]);
  not not_224 (not_224_out, irIN[6]);
  not not_225 (not_225_out, irIN[5]);
  not not_226 (not_226_out, irIN[4]);
  not not_227 (not_227_out, irIN[3]);
  not not_228 (not_228_out, irIN[2]);
  not not_229 (not_229_out, irIN[1]);
  not not_230 (not_230_out, irIN[0]);
  not not_231 (not_231_out, irIN[11]);
  not not_232 (not_232_out, irIN[10]);
  not not_233 (not_233_out, irIN[9]);
  not not_234 (not_234_out, irIN[8]);
  not not_235 (not_235_out, irIN[6]);
  not not_236 (not_236_out, irIN[5]);
  not not_237 (not_237_out, irIN[4]);
  not not_238 (not_238_out, irIN[3]);
  not not_239 (not_239_out, irIN[2]);
  not not_240 (not_240_out, irIN[1]);
  not not_241 (not_241_out, irIN[0]);
  not not_242 (not_242_out, irIN[11]);
  not not_243 (not_243_out, irIN[10]);
  not not_244 (not_244_out, irIN[9]);
  not not_245 (not_245_out, irIN[8]);
  not not_246 (not_246_out, irIN[7]);
  not not_247 (not_247_out, irIN[5]);
  not not_248 (not_248_out, irIN[4]);
  not not_249 (not_249_out, irIN[3]);
  not not_250 (not_250_out, irIN[2]);
  not not_251 (not_251_out, irIN[1]);
  not not_252 (not_252_out, irIN[0]);
  not not_253 (not_253_out, irIN[4]);
  Decoder #(.enable("false"), .select(4)) decoder_1 (
    .out0(decoder_1_out0), .out1(LOADB1), .out2(LOADB2), .out3(LOADB3), .out4(LOADB4), .out5(LOADB5),
    .out6(LOADB6), .out7(LOADB7), .out8(LOADB8), .out9(LOADB9), .out10(LOADB10), .out11(LOADB11),
    .out12(LOADB12), .out13(LOADB13), .out14(LOADB14), .out15(LOADB15), .sel(and_70_out));
  and and_72 (acLOAD5, alsuINSELECTOR2, irIN[11], not_187_out, not_188_out, not_189_out, not_190_out, not_191_out, not_192_out, not_193_out, not_194_out, not_195_out, not_196_out, not_197_out);
  and and_73 (OUTRLOAD, alsuINSELECTOR2, not_198_out, irIN[10], not_199_out, not_200_out, not_201_out, not_202_out, not_203_out, not_204_out, not_205_out, not_206_out, not_207_out, not_208_out);
  and and_74 (and_74_out, alsuINSELECTOR2, not_209_out, not_210_out, irIN[9], not_211_out, not_212_out, not_213_out, not_214_out, not_215_out, not_216_out, not_217_out, not_218_out, not_219_out);
  and and_75 (and_75_out, alsuINSELECTOR2, not_220_out, not_221_out, not_222_out, irIN[8], not_223_out, not_224_out, not_225_out, not_226_out, not_227_out, not_228_out, not_229_out, not_230_out);
  and and_76 (dIEN, alsuINSELECTOR2, not_231_out, not_232_out, not_233_out, not_234_out, irIN[7], not_235_out, not_236_out, not_237_out, not_238_out, not_239_out, not_240_out, not_241_out);
  and and_77 (IENCLR, alsuINSELECTOR2, not_242_out, not_243_out, not_244_out, not_245_out, not_246_out, irIN[6], not_247_out, not_248_out, not_249_out, not_250_out, not_251_out, not_252_out);
  and and_78 (S28, alsuINSELECTOR2, irIN[11], irIN[10], irIN[9], irIN[8], irIN[7], irIN[6], irIN[5], not_253_out);
  and and_79 (S33, irIN[3], drLOAD1);
  and and_80 (S25, irIN[2], drLOAD1);
  and and_81 (S17, irIN[1], drLOAD1);
  and and_82 (S07, irIN[0], drLOAD1);
  D_Flip_Flop d_ff_1 (.D(acLOAD5), .clk(CLK), .Q(inputFlush));  // open: Qn, preset, reset
  and and_83 (and_83_out, and_74_out, fgiOUT);
  and and_84 (and_84_out, fgoOUT, and_75_out);
  or or_31 (pcINCR5, and_83_out, and_84_out);
  _74175 #(.VccGndPorts("true")) u_74175_6 (
    .pin1(n74175_6_pin1), .pin2(fgoOUT), .pin4(dFGO), .pin8(GND), .pin16(VCC), .pin9(n74175_6_pin9));  // open: pin3, pin5, pin6, pin7, pin15, pin14, pin13, pin12, pin11, pin10
  and and_85 (n74175_6_pin9, FGOLOAD, CLK);
  not not_254 (n74175_6_pin1, or_32_out);
  buf or_32 (or_32_out, OUTRLOAD);  // OR_Gate
  buf or_33 (or_33_out, inputBufferNotEmpty);  // OR_Gate
  _74175 #(.VccGndPorts("true")) u_74175_7 (
    .pin1(n74175_7_pin1), .pin2(fgiOUT), .pin4(or_33_out), .pin8(GND), .pin16(VCC), .pin9(n74175_7_pin9));  // open: pin3, pin5, pin6, pin7, pin15, pin14, pin13, pin12, pin11, pin10
  and and_86 (n74175_7_pin9, or_34_out, CLK);
  buf or_34 (or_34_out, inputBufferNotEmpty);  // OR_Gate
  not not_255 (n74175_7_pin1, or_35_out);
  buf or_35 (or_35_out, acLOAD5);  // OR_Gate
  and and_87 (arLoad4, ROUT, T0);
  and and_88 (TRLOAD, ROUT, T1);
  and and_89 (S18, ROUT, T2);
  and and_90 (pcLOAD_t, ROUT, T3);
  and and_91 (IENCLR1, ROUT, T4);
  not not_256 (not_256_out, bit12AR);
  and and_92 (romWrite3, S18, not_256_out);
  and and_93 (ramWrite3, S18, bit12AR);

  // Other names for the same wires on the sheet: ACREG[15:0] = ACIN; acLOAD_t = ACCMPLMNT; alsuS01 = ACCMPLMNT;
  //   alsuS10 = ACCMPLMNT; alsuS21 = ACCMPLMNT; acLOAD1 = ACSHFR; alsuS30 = ACSHFR; acLOAD2 = ACSHFL;
  //   alsuS22 = ACSHFL; alsuS31 = ACSHFL; arBIT12 = bit12AR; S15 = arINCR_t; S10 = arLOAD; S09 = arLoad4;
  //   S34 = arLoad4; clearInputBuffer = inputFlush; CLKK = CLK; dFGI = inputBufferNotEmpty;
  //   FGILOAD = inputBufferNotEmpty; DRREG[15:0] = DRIN; EFLIPFLOP = EFLIPFLOPIN; eLOAD_t = ECMPLMNT; ienLOAD = dIEN;
  //   decode = arLOAD2; iLOAD = arLOAD2; S01 = arLOAD2; S21 = arLOAD2; irB0 = irIN[0]; irB1 = irIN[1]; irB2 = irIN[2];
  //   irB3 = irIN[3]; irB4 = irIN[4]; irB5 = irIN[5]; irB6 = irIN[6]; irB7 = irIN[7]; irB8 = irIN[8]; irB9 = irIN[9];
  //   irB10 = irIN[10]; irB11 = irIN[11]; qI = irIN[15]; alsuS20 = acLOAD3; mltDRINR = acLOAD3; alsuS00 = acLOAD4;
  //   eLOAD1 = acLOAD4; mltDRINR1 = acLOAD4; mltDRINR2 = acLOAD6; irLOAD = IRLD; pcINCR6 = IRLD; S04 = pcLOAD1;
  //   S08 = pcLOAD2; S010 = pcLOAD_t; S35 = pcLOAD_t; S00 = ramRead1; S11 = ramRead1; S20 = ramRead1; S03 = ramRead2;
  //   S13 = ramRead2; S23 = ramRead2; S02 = ramRead_t; S12 = ramRead_t; S22 = ramRead_t; S30 = romRead1;
  //   S32 = romRead2; S31 = romRead_t; S14 = TRLOAD; S16 = S05; S26 = OUTRLOAD; S27 = S18; scCLR5 = alsuINSELECTOR2;
  //   pcINCR8 = IENCLR1; rCLR = IENCLR1; scCLR10 = IENCLR1; mltDRINR3 = acLOAD7; scCLR11 = acLOAD7

  // Notes on the sheet:
  //   Write to rom or read from rom
  //   Write to ram or read from ram
  //   CLR
  //   D0
  //   I flipdlop
  //   Load
  //   S flipflop
  //   Load
  //   R flipflop
  //   Load
  //   ROUT
  //   delay 
  //   InDirect address
  //   halt computer
  //   Start of NON INTERUPT INSTRUCTION T0
  //   non Interupt T1
  //   non Interupt T2
  //   direct address
  //   register reference instruction execution begining
  //   clear ac signal
  //   clear E signal
  //   complement AC
  //   complement E
  //   shift right AC
  //   shift left AC
  //   increment ac
  //   PC address in bus
  //   ROM
  //   RAM
  //   skip next instruction if E is zero
  //   for future improvements
  //   skip next instruction if ac positive
  //   skip next instruction if ac negative
  //   skip next instruction if ac zero
  //   memory reference Instruction
  //   ROM
  //   RAM
  //   but now we do not need to do anything
  //   register or io reference instruction
  //   D7 & ~I & T3
  //   problem here
  //   loads 12 bit address to ar
  //   rom address in bus
  //   D7
  //   E is zero
  //   address of IR in bus
  //   ac is positive
  //   ac is negative
  //   ac zero
  //   ram address in bus
  //   rom address in bus
  //   ram address in bus
  //   AC is zero
  //   DR<- M[AR]
  //   ROM
  //   RAM
  //   rom address in bus
  //   ram address in bus
  //   and to ac
  //   Load to AC
  //   add to ac
  //   store AC
  //   branch save return address
  //   Branch unconditionally
  //   ROM
  //   RAM
  //   ROM
  //   RAM
  //   AR address in bus
  //   PC address in bus
  //   ar address in bus
  //   AC address in bus
  //   increment skip if zero
  //   ROM
  //   RAM
  //   DR is zero
  //   DR address in bus
  //   our own custom instructions (not in the book)
  //   FFFX
  //   PTA
  //   IEN out
  //   IO reference instruction
  //   IEN flipflop
  //   our own custom instructions (not in the book)
  //   our own custom instructions (not in the book)
  //   PTA
  //   Load
  //   peripheral to ac
  //   need to be completed
  //   INP
  //   OUT
  //   SKI
  //   SKO
  //   ION
  //   IOF
  //   FFEX
  //   ATP
  //   ac to peropheral
  //   peripheral address in bus
  //   ac address in bus
  //   AC address in bus
  //   FGO
  //   Load
  //   FGOOUT
  //   ECLR
  //   CLEAR NOT CONNECTED
  //   FGI
  //   Load
  //   FGIOUT
  //   ECLR
  //   pc <- address of the interrupt function
  //   M[AR] <- TR
  //   Interrupt instruction cycle
  //   RAM
  //   TR<-PC
  //   pc address in bus
  //   address of register that contain interrupt function address
  //   address of register that contain interrupt function address
  //   TR address in bus
endmodule
